// Digital circuit 16_bit_ALU_1.dig as structural Verilog
module _16_bit_ALU_1 (
  input  CLR,
  input  CLR_2,
  input  CLR_3,
  input  CLR_4,
  input  in_5,
  input  nCLR_AC,
  input  in_7,
  input  in_8,
  input  in_9,
  input  in_10,
  input  in_11,
  input  in_12,
  input  in_13,
  input  in_14,
  input  in_15,
  input  in_16,
  input  in_17,
  input  in_18,
  input  in_19,
  input  in_20,
  input  in_21,
  input  in_22,
  input  CLK,
  input  nSHL,
  input  nSHR,
  input  in_26,
  input  in_27,
  input  in_28,
  input  in_29,
  input  in_30,
  input  in_31,
  input  in_32,
  input  in_33
);

  wire AC0, AC1, AC2, AC3, AC4, AC5, AC6, AC7, AC8, AC9, AC10, AC11, AC12, AC13, AC14, AC15, ADD, AL, ALU0,
       ALU1, ALU2, ALU3, ALU4, ALU5, ALU6, ALU7, ALU8, ALU9, ALU10, ALU11, ALU12, ALU13, ALU14, ALU15, AND,
       AR0, AR1, AR2, AR3, C1, C7, C11, C15, diodebackward_1_out, diodebackward_3_out, diodebackward_15_out,
       LD, nJMP, OR, pullup_3_out, pullup_4_out, ST, SUB, U1_pin7, U1_pin9, U2_pin7, U2_pin9, U3_pin7,
       U3_pin9, U4_pin7, U4_pin9, U11_pin7, U11_pin9, U12_pin7, U12_pin9, U13_pin7, U13_pin9, U14_2_pin7,
       U14_2_pin9, U21_pin7, U21_pin9, U22_pin7, U22_pin9, U23_pin7, U23_pin9, U24_pin7, U24_pin9, U31_pin7,
       U31_pin9, U32_pin7, U32_pin9, U33_pin7, U33_pin9, U34_pin7, U34_pin9, XOR;

  _74138 U14 (
    .pin1(in_28), .pin2(in_29), .pin3(in_30), .pin4(1'b0), .pin5(1'b0), .pin6(1'b1), .pin7(nJMP),
    .pin8(1'b0), .pin9(ST), .pin10(SUB), .pin11(ADD), .pin12(XOR), .pin13(OR), .pin14(AND), .pin15(LD),
    .pin16(1'b1));
  DiodeBackward diodebackward_1 (.in(in_30), .out(diodebackward_1_out));
  DiodeBackward diodebackward_2 (.in(nJMP), .out(diodebackward_1_out));
  PullUp pullup_1 (.out(diodebackward_1_out));
  DiodeBackward diodebackward_3 (.in(LD), .out(diodebackward_3_out));
  DiodeBackward diodebackward_4 (.in(AND), .out(diodebackward_3_out));
  DiodeBackward diodebackward_5 (.in(OR), .out(diodebackward_3_out));
  DiodeBackward diodebackward_6 (.in(ADD), .out(diodebackward_3_out));
  PullUp pullup_2 (.out(diodebackward_3_out));
  PullUp pullup_3 (.out(pullup_3_out));
  DiodeBackward diodebackward_7 (.in(LD), .out(pullup_3_out));
  DiodeBackward diodebackward_8 (.in(OR), .out(pullup_3_out));
  DiodeBackward diodebackward_9 (.in(XOR), .out(pullup_3_out));
  DiodeBackward diodebackward_10 (.in(ADD), .out(pullup_3_out));
  DiodeBackward diodebackward_11 (.in(ST), .out(pullup_3_out));
  _74153 U4 (
    .pin1(1'b0), .pin2(in_19), .pin3(AR3), .pin4(AR2), .pin5(AR1), .pin6(AR0), .pin7(U4_pin7), .pin8(1'b0),
    .pin9(U4_pin9), .pin10(1'b0), .pin11(1'b1), .pin12(1'b0), .pin13(1'b1), .pin14(AC3), .pin15(AL),
    .pin16(1'b1));
  _74153 U3 (
    .pin1(1'b0), .pin2(in_20), .pin3(AR3), .pin4(AR2), .pin5(AR1), .pin6(AR0), .pin7(U3_pin7), .pin8(1'b0),
    .pin9(U3_pin9), .pin10(1'b0), .pin11(1'b1), .pin12(1'b0), .pin13(1'b1), .pin14(AC2), .pin15(AL),
    .pin16(1'b1));
  _74153 U2 (
    .pin1(1'b0), .pin2(in_21), .pin3(AR3), .pin4(AR2), .pin5(AR1), .pin6(AR0), .pin7(U2_pin7), .pin8(1'b0),
    .pin9(U2_pin9), .pin10(1'b0), .pin11(1'b1), .pin12(1'b0), .pin13(1'b1), .pin14(AC1), .pin15(AL),
    .pin16(1'b1));
  _74153 U1 (
    .pin1(1'b0), .pin2(in_22), .pin3(AR3), .pin4(AR2), .pin5(AR1), .pin6(AR0), .pin7(U1_pin7), .pin8(1'b0),
    .pin9(U1_pin9), .pin10(1'b0), .pin11(1'b1), .pin12(1'b0), .pin13(1'b1), .pin14(AC0), .pin15(AL),
    .pin16(1'b1));
  PullUp pullup_4 (.out(pullup_4_out));
  DiodeBackward diodebackward_12 (.in(OR), .out(pullup_4_out));
  DiodeBackward diodebackward_13 (.in(XOR), .out(pullup_4_out));
  DiodeBackward diodebackward_14 (.in(SUB), .out(pullup_4_out));
  DiodeBackward diodebackward_15 (.in(SUB), .out(diodebackward_15_out));
  DiodeBackward diodebackward_16 (.in(ST), .out(diodebackward_15_out));
  PullUp pullup_5 (.out(diodebackward_15_out));
  _74283 U26 (
    .pin1(ALU1), .pin2(U2_pin9), .pin3(U2_pin7), .pin4(ALU0), .pin5(U1_pin7), .pin6(U1_pin9), .pin7(AR0),
    .pin8(1'b0), .pin9(C1), .pin10(ALU3), .pin11(U4_pin9), .pin12(U4_pin7), .pin13(ALU2), .pin14(U3_pin7),
    .pin15(U3_pin9), .pin16(1'b1));
  _74540 U15 (
    .pin1(1'b0), .pin2(diodebackward_3_out), .pin3(pullup_3_out), .pin4(pullup_4_out),
    .pin5(diodebackward_15_out), .pin6(diodebackward_1_out), .pin7(1'b0), .pin8(1'b0), .pin9(1'b0),
    .pin10(1'b0), .pin14(AL), .pin15(AR0), .pin16(AR1), .pin17(AR2), .pin18(AR3), .pin19(1'b0), .pin20(1'b1));  // open: pin11, pin12, pin13
  _74173 U5 (
    .pin1(in_5), .pin2(in_5), .pin3(AC0), .pin4(AC1), .pin5(AC2), .pin6(AC3), .pin7(CLK), .pin8(1'b0),
    .pin9(in_33), .pin10(in_33), .pin11(ALU3), .pin12(ALU2), .pin13(ALU1), .pin14(ALU0), .pin15(CLR),
    .pin16(1'b1));
  Seven_Seg_Hex seven_seg_hex_1 (.d({in_7, in_8, in_9, in_10}), .dp(1'b0));
  Seven_Seg_Hex seven_seg_hex_2 (.d({in_11, in_12, in_13, in_14}), .dp(1'b0));
  Seven_Seg_Hex seven_seg_hex_3 (.d({in_15, in_16, in_17, in_18}), .dp(1'b0));
  Seven_Seg_Hex seven_seg_hex_4 (.d({in_19, in_20, in_21, in_22}), .dp(1'b0));
  _74153 U14_2 (
    .pin1(1'b0), .pin2(in_15), .pin3(AR3), .pin4(AR2), .pin5(AR1), .pin6(AR0), .pin7(U14_2_pin7),
    .pin8(1'b0), .pin9(U14_2_pin9), .pin10(1'b0), .pin11(1'b1), .pin12(1'b0), .pin13(1'b1), .pin14(AC7),
    .pin15(AL), .pin16(1'b1));
  _74153 U13 (
    .pin1(1'b0), .pin2(in_16), .pin3(AR3), .pin4(AR2), .pin5(AR1), .pin6(AR0), .pin7(U13_pin7), .pin8(1'b0),
    .pin9(U13_pin9), .pin10(1'b0), .pin11(1'b1), .pin12(1'b0), .pin13(1'b1), .pin14(AC6), .pin15(AL),
    .pin16(1'b1));
  _74153 U12 (
    .pin1(1'b0), .pin2(in_17), .pin3(AR3), .pin4(AR2), .pin5(AR1), .pin6(AR0), .pin7(U12_pin7), .pin8(1'b0),
    .pin9(U12_pin9), .pin10(1'b0), .pin11(1'b1), .pin12(1'b0), .pin13(1'b1), .pin14(AC5), .pin15(AL),
    .pin16(1'b1));
  _74153 U11 (
    .pin1(1'b0), .pin2(in_18), .pin3(AR3), .pin4(AR2), .pin5(AR1), .pin6(AR0), .pin7(U11_pin7), .pin8(1'b0),
    .pin9(U11_pin9), .pin10(1'b0), .pin11(1'b1), .pin12(1'b0), .pin13(1'b1), .pin14(AC4), .pin15(AL),
    .pin16(1'b1));
  Seven_Seg_Hex seven_seg_hex_5 (.d({AC15, AC14, AC13, AC12}), .dp(1'b0));
  Seven_Seg_Hex seven_seg_hex_6 (.d({AC11, AC10, AC9, AC8}), .dp(1'b0));
  _74283 U25 (
    .pin1(ALU5), .pin2(U12_pin9), .pin3(U12_pin7), .pin4(ALU4), .pin5(U11_pin7), .pin6(U11_pin9), .pin7(C1),
    .pin8(1'b0), .pin9(C7), .pin10(ALU7), .pin11(U14_2_pin9), .pin12(U14_2_pin7), .pin13(ALU6),
    .pin14(U13_pin7), .pin15(U13_pin9), .pin16(1'b1));
  Seven_Seg_Hex seven_seg_hex_7 (.d({AC7, AC6, AC5, AC4}), .dp(1'b0));
  Seven_Seg_Hex seven_seg_hex_8 (.d({AC3, AC2, AC1, AC0}), .dp(1'b0));
  _74173 U15_2 (
    .pin1(in_5), .pin2(in_5), .pin3(AC4), .pin4(AC5), .pin5(AC6), .pin6(AC7), .pin7(CLK), .pin8(1'b0),
    .pin9(in_33), .pin10(in_33), .pin11(ALU7), .pin12(ALU6), .pin13(ALU5), .pin14(ALU4), .pin15(CLR_2),
    .pin16(1'b1));
  Seven_Seg_Hex seven_seg_hex_9 (.d({ALU15, ALU14, ALU13, ALU12}), .dp(1'b0));
  _74153 U24 (
    .pin1(1'b0), .pin2(in_11), .pin3(AR3), .pin4(AR2), .pin5(AR1), .pin6(AR0), .pin7(U24_pin7), .pin8(1'b0),
    .pin9(U24_pin9), .pin10(1'b0), .pin11(1'b1), .pin12(1'b0), .pin13(1'b1), .pin14(AC11), .pin15(AL),
    .pin16(1'b1));
  _74153 U23 (
    .pin1(1'b0), .pin2(in_12), .pin3(AR3), .pin4(AR2), .pin5(AR1), .pin6(AR0), .pin7(U23_pin7), .pin8(1'b0),
    .pin9(U23_pin9), .pin10(1'b0), .pin11(1'b1), .pin12(1'b0), .pin13(1'b1), .pin14(AC10), .pin15(AL),
    .pin16(1'b1));
  _74153 U22 (
    .pin1(1'b0), .pin2(in_13), .pin3(AR3), .pin4(AR2), .pin5(AR1), .pin6(AR0), .pin7(U22_pin7), .pin8(1'b0),
    .pin9(U22_pin9), .pin10(1'b0), .pin11(1'b1), .pin12(1'b0), .pin13(1'b1), .pin14(AC9), .pin15(AL),
    .pin16(1'b1));
  _74153 U21 (
    .pin1(1'b0), .pin2(in_14), .pin3(AR3), .pin4(AR2), .pin5(AR1), .pin6(AR0), .pin7(U21_pin7), .pin8(1'b0),
    .pin9(U21_pin9), .pin10(1'b0), .pin11(1'b1), .pin12(1'b0), .pin13(1'b1), .pin14(AC8), .pin15(AL),
    .pin16(1'b1));
  Seven_Seg_Hex seven_seg_hex_10 (.d({ALU11, ALU10, ALU9, ALU8}), .dp(1'b0));
  Seven_Seg_Hex seven_seg_hex_11 (.d({ALU7, ALU6, ALU5, ALU4}), .dp(1'b0));
  Seven_Seg_Hex seven_seg_hex_12 (.d({ALU3, ALU2, ALU1, ALU0}), .dp(1'b0));
  _74283 U28 (
    .pin1(ALU9), .pin2(U22_pin9), .pin3(U22_pin7), .pin4(ALU8), .pin5(U21_pin7), .pin6(U21_pin9), .pin7(C7),
    .pin8(1'b0), .pin9(C11), .pin10(ALU11), .pin11(U24_pin9), .pin12(U24_pin7), .pin13(ALU10),
    .pin14(U23_pin7), .pin15(U23_pin9), .pin16(1'b1));
  _74173 U25_2 (
    .pin1(in_5), .pin2(in_5), .pin3(AC8), .pin4(AC9), .pin5(AC10), .pin6(AC11), .pin7(CLK), .pin8(1'b0),
    .pin9(in_33), .pin10(in_33), .pin11(ALU11), .pin12(ALU10), .pin13(ALU9), .pin14(ALU8), .pin15(CLR_3),
    .pin16(1'b1));
  _74153 U34 (
    .pin1(1'b0), .pin2(in_7), .pin3(AR3), .pin4(AR2), .pin5(AR1), .pin6(AR0), .pin7(U34_pin7), .pin8(1'b0),
    .pin9(U34_pin9), .pin10(1'b0), .pin11(1'b1), .pin12(1'b0), .pin13(1'b1), .pin14(AC15), .pin15(AL),
    .pin16(1'b1));
  _74153 U33 (
    .pin1(1'b0), .pin2(in_8), .pin3(AR3), .pin4(AR2), .pin5(AR1), .pin6(AR0), .pin7(U33_pin7), .pin8(1'b0),
    .pin9(U33_pin9), .pin10(1'b0), .pin11(1'b1), .pin12(1'b0), .pin13(1'b1), .pin14(AC14), .pin15(AL),
    .pin16(1'b1));
  _74153 U32 (
    .pin1(1'b0), .pin2(in_9), .pin3(AR3), .pin4(AR2), .pin5(AR1), .pin6(AR0), .pin7(U32_pin7), .pin8(1'b0),
    .pin9(U32_pin9), .pin10(1'b0), .pin11(1'b1), .pin12(1'b0), .pin13(1'b1), .pin14(AC13), .pin15(AL),
    .pin16(1'b1));
  _74153 U31 (
    .pin1(1'b0), .pin2(in_10), .pin3(AR3), .pin4(AR2), .pin5(AR1), .pin6(AR0), .pin7(U31_pin7), .pin8(1'b0),
    .pin9(U31_pin9), .pin10(1'b0), .pin11(1'b1), .pin12(1'b0), .pin13(1'b1), .pin14(AC12), .pin15(AL),
    .pin16(1'b1));
  _74283 U27 (
    .pin1(ALU13), .pin2(U32_pin9), .pin3(U32_pin7), .pin4(ALU12), .pin5(U31_pin7), .pin6(U31_pin9),
    .pin7(C11), .pin8(1'b0), .pin9(C15), .pin10(ALU15), .pin11(U34_pin9), .pin12(U34_pin7), .pin13(ALU14),
    .pin14(U33_pin7), .pin15(U33_pin9), .pin16(1'b1));
  LED led_1 (.in(C15));
  _74173 U35 (
    .pin1(in_5), .pin2(in_5), .pin3(AC12), .pin4(AC13), .pin5(AC14), .pin6(AC15), .pin7(CLK), .pin8(1'b0),
    .pin9(in_33), .pin10(in_33), .pin11(ALU15), .pin12(ALU14), .pin13(ALU13), .pin14(ALU12), .pin15(CLR_4),
    .pin16(1'b1));
  _74194 _74194_1 (
    .pin1(nCLR_AC), .pin2(in_27), .pin3(ALU0), .pin4(ALU1), .pin5(ALU2), .pin6(ALU3), .pin7(AC4),
    .pin8(1'b0), .pin9(nSHR), .pin10(nSHL), .pin11(CLK), .pin12(AC3), .pin13(AC2), .pin14(AC1), .pin15(AC0),
    .pin16(1'b1));
  _74194 _74194_2 (
    .pin1(nCLR_AC), .pin2(AC3), .pin3(ALU4), .pin4(ALU5), .pin5(ALU6), .pin6(ALU7), .pin7(AC8), .pin8(1'b0),
    .pin9(nSHR), .pin10(nSHL), .pin11(CLK), .pin12(AC7), .pin13(AC6), .pin14(AC5), .pin15(AC4), .pin16(1'b1));
  _74194 _74194_3 (
    .pin1(nCLR_AC), .pin2(AC7), .pin3(ALU8), .pin4(ALU9), .pin5(ALU10), .pin6(ALU11), .pin7(AC12),
    .pin8(1'b0), .pin9(nSHR), .pin10(nSHL), .pin11(CLK), .pin12(AC11), .pin13(AC10), .pin14(AC9),
    .pin15(AC8), .pin16(1'b1));
  _74194 _74194_4 (
    .pin1(nCLR_AC), .pin2(AC11), .pin3(ALU12), .pin4(ALU13), .pin5(ALU14), .pin6(ALU15), .pin7(in_26),
    .pin8(1'b0), .pin9(nSHR), .pin10(nSHL), .pin11(CLK), .pin12(AC15), .pin13(AC14), .pin14(AC13),
    .pin15(AC12), .pin16(1'b1));

  // Other names for the same wires on the sheet: BUS0 = in_22; BUS1 = in_21; BUS2 = in_20; BUS3 = in_19; BUS4 = in_18;
  //   BUS5 = in_17; BUS6 = in_16; BUS7 = in_15; BUS8 = in_14; BUS9 = in_13; BUS10 = in_12; BUS11 = in_11;
  //   BUS12 = in_10; BUS13 = in_9; BUS14 = in_8; BUS15 = in_7; CL_AC = nCLR_AC; CLK1 = CLK; CLK2 = CLK; IR5 = in_28;
  //   IR6 = in_29; IR7 = in_30; nEN = in_5; nLD = in_33; S0 = nSHR; S1 = nSHL; SL = in_26; SR = in_27

  // Notes on the sheet:
  //   in_5: default 1
  //   ALU + Accumulator
  //   ALU-0
  //   MUX3
  //   MUX2
  //   MUX1
  //   MUX0
  //   LOAD
  //   AND
  //   OR
  //   XOR
  //   ADD
  //   SUB
  //   STORE
  //   JMP
  //   ACCUMULATOR
  //   ADDER
  //   ALU-1
  //   BUS DATA
  //   MUX7
  //   MUX6
  //   MUX5
  //   MUX4
  //   ACC
  //   0  LOAD
  //   1  AND
  //   2  OR
  //   3  XOR
  //   4  ADD
  //   5  SUB
  //   6  STORE
  //   7  JMP
  //   ALU-2
  //   ALU OUT
  //   ALU-3
  //   Cout
endmodule
