// Digital circuit 16_bit_ALU_4.dig as structural Verilog
module _16_bit_ALU_4 (
  input  nCLR_AC,
  input  CLK,
  input  in_3,
  input  in_4,
  input  in_5,
  input  in_6,
  input  nEN,
  input  in_8,
  input  in_9
);

  wire _0_out, _1_out, _2_out, _3_out, _4_out, _5_out, _6_out, _7_out, _8_out, _9_out, _74173_4_pin11,
       _74173_4_pin12, _74173_4_pin13, _74173_4_pin14, _74193_1_pin12, _74193_1_pin13, _74193_2_pin12,
       _74193_2_pin13, _74193_3_pin12, _74193_3_pin13, _74540_1_pin11, _74540_1_pin12, _74540_1_pin13,
       _74540_1_pin14, _74540_1_pin15, _74540_1_pin16, _74540_1_pin17, A0, A1, A2, A3, A4, A5, A6, A7, A8,
       A9, A10, A11, A12, A13, A14, A15, A_out, AC0, AC1, AC2, AC3, AC4, AC5, AC6, AC7, AC8, AC9, AC10, AC11,
       AC12, AC13, AC14, AC15, ADD, Address_out, AL, ALU, ALU0, ALU1, ALU2, ALU3, ALU4, ALU5, ALU6, ALU7,
       ALU8, ALU9, ALU10, ALU11, ALU12, ALU13, ALU14, ALU15, ALU_to_RAM_out, AND, AR0, AR1, AR2, AR3, B_out,
       BUS0, BUS1, BUS2, BUS3, BUS4, BUS5, BUS6, BUS7, BUS8, BUS9, BUS10, BUS11, BUS12, BUS13, BUS14, BUS15,
       C0, C1, C7, C11, C15, C_out, Clear_out, CLK_t, D_out, Dec_out, Deposit_WR_out, diodebackward_1_out,
       diodebackward_2_out, diodebackward_4_out, diodebackward_11_out, diodebackward_13_out,
       diodebackward_25_out, diodebackward_40_out, diodebackward_51_out, diodebackward_53_out,
       diodebackward_58_out, diodebackward_62_out, diodebackward_73_out, diodebackward_88_out,
       diodeforward_1_out, DN, E_out, Examine_RD_out, F1, F2, F3, F4, F_out, Inc_out, LD, nALB, nDE, nJMP,
       nLD, nOE, not_1_out, not_4_out, not_10_out, nWE, OR, pullup_2_out, pullup_4_out, pullup_5_out,
       pullup_8_out, pullup_9_out, pullup_11_out, pullup_15_out, pullup_16_out, pullup_19_out, pullup_20_out,
       pullup_22_out, pullup_23_out, pullup_26_out, Q0, Q1, Q2, Q3, Q4, Q5, Q6, Q7, Q8, Q9, Q10, Q11, Q12,
       Q13, Q14, Q15, RES, ROL, ROR, S0, S1, SL, SR, ST, STR, SUB, U1_pin7, U1_pin9, U2_pin7, U2_pin9,
       U3_pin7, U3_pin9, U4_pin7, U4_pin9, U11_pin7, U11_pin9, U12_pin7, U12_pin9, U13_pin7, U13_pin9,
       U14_2_pin7, U14_2_pin9, U16_2_pin11, U16_2_pin12, U16_2_pin13, U16_pin7, U16_pin9, U16_pin10,
       U16_pin11, U16_pin12, U16_pin13, U16_pin14, U16_pin15, U21_pin7, U21_pin9, U22_pin7, U22_pin9,
       U23_pin7, U23_pin9, U24_pin7, U24_pin9, U31_pin7, U31_pin9, U32_pin7, U32_pin9, U33_pin7, U33_pin9,
       U34_pin7, U34_pin9, UP, XOR;

  _74153 U4 (
    .pin1(1'b0), .pin2(BUS3), .pin3(AR3), .pin4(AR2), .pin5(AR1), .pin6(AR0), .pin7(U4_pin7), .pin8(1'b0),
    .pin9(U4_pin9), .pin10(F1), .pin11(F2), .pin12(F3), .pin13(F4), .pin14(AC3), .pin15(AL), .pin16(1'b1));
  _74153 U3 (
    .pin1(1'b0), .pin2(BUS2), .pin3(AR3), .pin4(AR2), .pin5(AR1), .pin6(AR0), .pin7(U3_pin7), .pin8(1'b0),
    .pin9(U3_pin9), .pin10(F1), .pin11(F2), .pin12(F3), .pin13(F4), .pin14(AC2), .pin15(AL), .pin16(1'b1));
  _74153 U2 (
    .pin1(1'b0), .pin2(BUS1), .pin3(AR3), .pin4(AR2), .pin5(AR1), .pin6(AR0), .pin7(U2_pin7), .pin8(1'b0),
    .pin9(U2_pin9), .pin10(F1), .pin11(F2), .pin12(F3), .pin13(F4), .pin14(AC1), .pin15(AL), .pin16(1'b1));
  _74153 U1 (
    .pin1(1'b0), .pin2(BUS0), .pin3(AR3), .pin4(AR2), .pin5(AR1), .pin6(AR0), .pin7(U1_pin7), .pin8(1'b0),
    .pin9(U1_pin9), .pin10(F1), .pin11(F2), .pin12(F3), .pin13(F4), .pin14(AC0), .pin15(AL), .pin16(1'b1));
  _74138 U14 (
    .pin1(in_6), .pin2(in_3), .pin3(in_4), .pin4(in_5), .pin5(nEN), .pin6(1'b1), .pin7(nJMP), .pin8(1'b0),
    .pin9(ST), .pin10(SUB), .pin11(ADD), .pin12(XOR), .pin13(OR), .pin14(AND), .pin15(LD), .pin16(1'b1));
  _74138 U16 (
    .pin1(in_6), .pin2(in_3), .pin3(in_4), .pin4(1'b0), .pin5(nEN), .pin6(in_5), .pin7(U16_pin7),
    .pin8(1'b0), .pin9(U16_pin9), .pin10(U16_pin10), .pin11(U16_pin11), .pin12(U16_pin12), .pin13(U16_pin13),
    .pin14(U16_pin14), .pin15(U16_pin15), .pin16(1'b1));
  DiodeBackward diodebackward_1 (.in(U16_pin11), .out(diodebackward_1_out));
  PullUp pullup_1 (.out(diodebackward_1_out));
  DiodeBackward diodebackward_2 (.in(U16_pin10), .out(diodebackward_2_out));
  _74283 U26 (
    .pin1(ALU1), .pin2(U2_pin9), .pin3(U2_pin7), .pin4(ALU0), .pin5(U1_pin7), .pin6(U1_pin9), .pin7(C0),
    .pin8(1'b0), .pin9(C1), .pin10(ALU3), .pin11(U4_pin9), .pin12(U4_pin7), .pin13(ALU2), .pin14(U3_pin7),
    .pin15(U3_pin9), .pin16(1'b1));
  PullUp pullup_2 (.out(pullup_2_out));
  DiodeBackward diodebackward_3 (.in(SUB), .out(pullup_2_out));
  PullUp pullup_3 (.out(diodebackward_2_out));
  PullUp pullup_4 (.out(pullup_4_out));
  PullUp pullup_5 (.out(pullup_5_out));
  DiodeBackward diodebackward_4 (.in(LD), .out(diodebackward_4_out));
  DiodeBackward diodebackward_5 (.in(AND), .out(diodebackward_4_out));
  DiodeBackward diodebackward_6 (.in(OR), .out(diodebackward_4_out));
  DiodeBackward diodebackward_7 (.in(ADD), .out(diodebackward_4_out));
  DiodeBackward diodebackward_8 (.in(nJMP), .out(pullup_5_out));
  DiodeBackward diodebackward_9 (.in(in_4), .out(pullup_5_out));
  DiodeBackward diodebackward_10 (.in(U16_pin11), .out(diodebackward_4_out));
  DiodeBackward diodebackward_11 (.in(U16_pin11), .out(diodebackward_11_out));
  DiodeBackward diodebackward_12 (.in(U16_pin10), .out(diodebackward_4_out));
  PullUp pullup_6 (.out(diodebackward_4_out));
  DiodeBackward diodebackward_13 (.in(LD), .out(diodebackward_13_out));
  DiodeBackward diodebackward_14 (.in(OR), .out(diodebackward_13_out));
  DiodeBackward diodebackward_15 (.in(XOR), .out(diodebackward_13_out));
  DiodeBackward diodebackward_16 (.in(ADD), .out(diodebackward_13_out));
  DiodeBackward diodebackward_17 (.in(ST), .out(diodebackward_13_out));
  DiodeBackward diodebackward_18 (.in(U16_pin11), .out(diodebackward_13_out));
  DiodeBackward diodebackward_19 (.in(U16_pin10), .out(diodebackward_13_out));
  DiodeBackward diodebackward_20 (.in(U16_pin7), .out(diodebackward_13_out));
  PullUp pullup_7 (.out(diodebackward_13_out));
  PullUp pullup_8 (.out(pullup_8_out));
  DiodeBackward diodebackward_21 (.in(OR), .out(pullup_8_out));
  DiodeBackward diodebackward_22 (.in(XOR), .out(pullup_8_out));
  DiodeBackward diodebackward_23 (.in(SUB), .out(pullup_8_out));
  PullUp pullup_9 (.out(pullup_9_out));
  DiodeBackward diodebackward_24 (.in(U16_pin12), .out(pullup_9_out));
  _74194 _74194_1 (
    .pin1(nCLR_AC), .pin2(SR), .pin3(ALU0), .pin4(ALU1), .pin5(ALU2), .pin6(ALU3), .pin7(AC4), .pin8(1'b0),
    .pin9(S0), .pin10(S1), .pin11(CLK), .pin12(AC3), .pin13(AC2), .pin14(AC1), .pin15(AC0), .pin16(1'b1));
  PullUp pullup_10 (.out(diodebackward_11_out));
  DiodeBackward diodebackward_25 (.in(LD), .out(diodebackward_25_out));
  DiodeBackward diodebackward_26 (.in(AND), .out(diodebackward_25_out));
  DiodeBackward diodebackward_27 (.in(OR), .out(diodebackward_25_out));
  DiodeBackward diodebackward_28 (.in(XOR), .out(diodebackward_25_out));
  DiodeBackward diodebackward_29 (.in(ADD), .out(diodebackward_25_out));
  DiodeBackward diodebackward_30 (.in(SUB), .out(diodebackward_11_out));
  DiodeBackward diodebackward_31 (.in(SUB), .out(diodebackward_25_out));
  DiodeBackward diodebackward_32 (.in(ST), .out(diodebackward_11_out));
  DiodeBackward diodebackward_33 (.in(ST), .out(diodebackward_25_out));
  DiodeBackward diodebackward_34 (.in(nJMP), .out(diodebackward_25_out));
  PullUp pullup_11 (.out(pullup_11_out));
  DiodeBackward diodebackward_35 (.in(U16_pin15), .out(diodebackward_25_out));
  DiodeBackward diodebackward_36 (.in(U16_pin13), .out(diodebackward_25_out));
  DiodeBackward diodebackward_37 (.in(U16_pin13), .out(pullup_11_out));
  DiodeBackward diodebackward_38 (.in(U16_pin7), .out(diodebackward_25_out));
  DiodeBackward diodebackward_39 (.in(U16_pin7), .out(pullup_11_out));
  PullUp pullup_12 (.out(diodebackward_25_out));
  DiodeBackward diodebackward_40 (.in(LD), .out(diodebackward_40_out));
  DiodeBackward diodebackward_41 (.in(AND), .out(diodebackward_40_out));
  DiodeBackward diodebackward_42 (.in(OR), .out(diodebackward_40_out));
  DiodeBackward diodebackward_43 (.in(XOR), .out(diodebackward_40_out));
  DiodeBackward diodebackward_44 (.in(ADD), .out(diodebackward_40_out));
  DiodeBackward diodebackward_45 (.in(SUB), .out(diodebackward_40_out));
  DiodeBackward diodebackward_46 (.in(ST), .out(diodebackward_40_out));
  DiodeBackward diodebackward_47 (.in(nJMP), .out(diodebackward_40_out));
  DiodeBackward diodebackward_48 (.in(U16_pin14), .out(diodebackward_40_out));
  DiodeBackward diodebackward_49 (.in(U16_pin12), .out(diodebackward_40_out));
  DiodeBackward diodebackward_50 (.in(U16_pin7), .out(diodebackward_40_out));
  PullUp pullup_13 (.out(diodebackward_40_out));
  _74540 U15 (
    .pin1(1'b0), .pin2(diodebackward_4_out), .pin3(diodebackward_13_out), .pin4(pullup_8_out),
    .pin5(diodebackward_11_out), .pin6(pullup_5_out), .pin7(pullup_2_out), .pin8(1'b0), .pin9(1'b0),
    .pin10(1'b0), .pin13(AR0), .pin14(AL), .pin15(C0), .pin16(AR1), .pin17(AR2), .pin18(AR3), .pin19(1'b0),
    .pin20(1'b1));  // open: pin11, pin12
  _74540 U16_2 (
    .pin1(1'b0), .pin2(diodebackward_40_out), .pin3(diodebackward_25_out), .pin4(pullup_11_out),
    .pin5(pullup_9_out), .pin6(diodebackward_13_out), .pin7(pullup_4_out), .pin8(diodebackward_2_out),
    .pin9(diodebackward_1_out), .pin10(1'b0), .pin11(U16_2_pin11), .pin12(U16_2_pin12), .pin13(U16_2_pin13),
    .pin14(STR), .pin15(ROL), .pin16(ROR), .pin17(S0), .pin18(S1), .pin19(1'b0), .pin20(1'b1));
  Seven_Seg_Hex seven_seg_hex_1 (.d({BUS15, BUS14, BUS13, BUS12}), .dp(1'b0));
  _74153 U14_2 (
    .pin1(1'b0), .pin2(BUS7), .pin3(AR3), .pin4(AR2), .pin5(AR1), .pin6(AR0), .pin7(U14_2_pin7), .pin8(1'b0),
    .pin9(U14_2_pin9), .pin10(F1), .pin11(F2), .pin12(F3), .pin13(F4), .pin14(AC7), .pin15(AL), .pin16(1'b1));
  _74153 U13 (
    .pin1(1'b0), .pin2(BUS6), .pin3(AR3), .pin4(AR2), .pin5(AR1), .pin6(AR0), .pin7(U13_pin7), .pin8(1'b0),
    .pin9(U13_pin9), .pin10(F1), .pin11(F2), .pin12(F3), .pin13(F4), .pin14(AC6), .pin15(AL), .pin16(1'b1));
  _74153 U12 (
    .pin1(1'b0), .pin2(BUS5), .pin3(AR3), .pin4(AR2), .pin5(AR1), .pin6(AR0), .pin7(U12_pin7), .pin8(1'b0),
    .pin9(U12_pin9), .pin10(F1), .pin11(F2), .pin12(F3), .pin13(F4), .pin14(AC5), .pin15(AL), .pin16(1'b1));
  _74153 U11 (
    .pin1(1'b0), .pin2(BUS4), .pin3(AR3), .pin4(AR2), .pin5(AR1), .pin6(AR0), .pin7(U11_pin7), .pin8(1'b0),
    .pin9(U11_pin9), .pin10(F1), .pin11(F2), .pin12(F3), .pin13(F4), .pin14(AC4), .pin15(AL), .pin16(1'b1));
  Seven_Seg_Hex seven_seg_hex_2 (.d({BUS11, BUS10, BUS9, BUS8}), .dp(1'b0));
  DiodeForward diodeforward_1 (.in(ALU0), .out(diodeforward_1_out));
  DiodeForward diodeforward_2 (.in(ALU1), .out(diodeforward_1_out));
  DiodeForward diodeforward_3 (.in(ALU2), .out(diodeforward_1_out));
  DiodeForward diodeforward_4 (.in(ALU3), .out(diodeforward_1_out));
  DiodeForward diodeforward_5 (.in(ALU4), .out(diodeforward_1_out));
  DiodeForward diodeforward_6 (.in(ALU5), .out(diodeforward_1_out));
  DiodeForward diodeforward_7 (.in(ALU6), .out(diodeforward_1_out));
  DiodeForward diodeforward_8 (.in(ALU7), .out(diodeforward_1_out));
  DiodeForward diodeforward_9 (.in(ALU8), .out(diodeforward_1_out));
  DiodeForward diodeforward_10 (.in(ALU9), .out(diodeforward_1_out));
  DiodeForward diodeforward_11 (.in(ALU10), .out(diodeforward_1_out));
  DiodeForward diodeforward_12 (.in(ALU11), .out(diodeforward_1_out));
  DiodeForward diodeforward_13 (.in(ALU12), .out(diodeforward_1_out));
  DiodeForward diodeforward_14 (.in(ALU13), .out(diodeforward_1_out));
  DiodeForward diodeforward_15 (.in(ALU14), .out(diodeforward_1_out));
  DiodeForward diodeforward_16 (.in(ALU15), .out(diodeforward_1_out));
  and and_1 (SL, AC0, ROL);
  and and_2 (SR, AC15, ROR);
  xor xor_1 (F4, 1'b1, U16_2_pin11);
  xor xor_2 (F3, 1'b0, U16_2_pin12);
  xor xor_3 (F2, 1'b1, U16_2_pin11);
  xor xor_4 (F1, 1'b0, U16_2_pin12);
  Seven_Seg_Hex seven_seg_hex_3 (.d({BUS7, BUS6, BUS5, BUS4}), .dp(1'b0));
  not not_1 (not_1_out, diodeforward_1_out);
  PullDown pulldown_1 (.out(diodeforward_1_out));
  Seven_Seg_Hex seven_seg_hex_4 (.d({BUS3, BUS2, BUS1, BUS0}), .dp(1'b0));
  LED ALU_ZERO (.in(not_1_out));
  _74283 U25 (
    .pin1(ALU5), .pin2(U12_pin9), .pin3(U12_pin7), .pin4(ALU4), .pin5(U11_pin7), .pin6(U11_pin9), .pin7(C1),
    .pin8(1'b0), .pin9(C7), .pin10(ALU7), .pin11(U14_2_pin9), .pin12(U14_2_pin7), .pin13(ALU6),
    .pin14(U13_pin7), .pin15(U13_pin9), .pin16(1'b1));
  _74194 _74194_2 (
    .pin1(nCLR_AC), .pin2(AC3), .pin3(ALU4), .pin4(ALU5), .pin5(ALU6), .pin6(ALU7), .pin7(AC8), .pin8(1'b0),
    .pin9(S0), .pin10(S1), .pin11(CLK), .pin12(AC7), .pin13(AC6), .pin14(AC5), .pin15(AC4), .pin16(1'b1));
  Seven_Seg_Hex seven_seg_hex_5 (.d({AC15, AC14, AC13, AC12}), .dp(1'b0));
  Seven_Seg_Hex seven_seg_hex_6 (.d({AC11, AC10, AC9, AC8}), .dp(1'b0));
  Seven_Seg_Hex seven_seg_hex_7 (.d({AC7, AC6, AC5, AC4}), .dp(1'b0));
  Seven_Seg_Hex seven_seg_hex_8 (.d({AC3, AC2, AC1, AC0}), .dp(1'b0));
  Seven_Seg_Hex seven_seg_hex_9 (.d({ALU15, ALU14, ALU13, ALU12}), .dp(1'b0));
  Seven_Seg_Hex seven_seg_hex_10 (.d({ALU11, ALU10, ALU9, ALU8}), .dp(1'b0));
  Seven_Seg_Hex seven_seg_hex_11 (.d({ALU7, ALU6, ALU5, ALU4}), .dp(1'b0));
  Seven_Seg_Hex seven_seg_hex_12 (.d({ALU3, ALU2, ALU1, ALU0}), .dp(1'b0));
  _74153 U24 (
    .pin1(1'b0), .pin2(BUS11), .pin3(AR3), .pin4(AR2), .pin5(AR1), .pin6(AR0), .pin7(U24_pin7), .pin8(1'b0),
    .pin9(U24_pin9), .pin10(F1), .pin11(F2), .pin12(F3), .pin13(F4), .pin14(AC11), .pin15(AL), .pin16(1'b1));
  _74153 U23 (
    .pin1(1'b0), .pin2(BUS10), .pin3(AR3), .pin4(AR2), .pin5(AR1), .pin6(AR0), .pin7(U23_pin7), .pin8(1'b0),
    .pin9(U23_pin9), .pin10(F1), .pin11(F2), .pin12(F3), .pin13(F4), .pin14(AC10), .pin15(AL), .pin16(1'b1));
  _74153 U22 (
    .pin1(1'b0), .pin2(BUS9), .pin3(AR3), .pin4(AR2), .pin5(AR1), .pin6(AR0), .pin7(U22_pin7), .pin8(1'b0),
    .pin9(U22_pin9), .pin10(F1), .pin11(F2), .pin12(F3), .pin13(F4), .pin14(AC9), .pin15(AL), .pin16(1'b1));
  _74153 U21 (
    .pin1(1'b0), .pin2(BUS8), .pin3(AR3), .pin4(AR2), .pin5(AR1), .pin6(AR0), .pin7(U21_pin7), .pin8(1'b0),
    .pin9(U21_pin9), .pin10(F1), .pin11(F2), .pin12(F3), .pin13(F4), .pin14(AC8), .pin15(AL), .pin16(1'b1));
  DiodeBackward diodebackward_51 (.in(Address_out), .out(diodebackward_51_out));
  PullUp pullup_14 (.out(diodebackward_51_out));
  PullUp pullup_15 (.out(pullup_15_out));
  DiodeBackward diodebackward_52 (.in(Dec_out), .out(pullup_15_out));
  not not_2 (nLD, _74540_1_pin11);
  _74139 _74139_1 (
    .pin1(1'b1), .pin2(1'b1), .pin3(1'b1), .pin8(1'b0), .pin11(nALB), .pin12(nDE), .pin13(1'b0), .pin14(ALU),
    .pin15(nWE), .pin16(1'b1));  // open: pin4, pin5, pin6, pin7, pin9, pin10
  PullUp pullup_16 (.out(pullup_16_out));
  DiodeBackward diodebackward_53 (.in(ALU_to_RAM_out), .out(diodebackward_53_out));
  DiodeBackward diodebackward_54 (.in(Examine_RD_out), .out(diodebackward_53_out));
  DiodeBackward diodebackward_55 (.in(Dec_out), .out(diodebackward_53_out));
  DiodeBackward diodebackward_56 (.in(Inc_out), .out(pullup_16_out));
  DiodeBackward diodebackward_57 (.in(Inc_out), .out(diodebackward_53_out));
  PullUp pullup_17 (.out(diodebackward_53_out));
  DiodeBackward diodebackward_58 (.in(Examine_RD_out), .out(diodebackward_58_out));
  DiodeBackward diodebackward_59 (.in(Deposit_WR_out), .out(diodebackward_58_out));
  not not_3 (ALU, _74540_1_pin15);
  _74283 U28 (
    .pin1(ALU9), .pin2(U22_pin9), .pin3(U22_pin7), .pin4(ALU8), .pin5(U21_pin7), .pin6(U21_pin9), .pin7(C7),
    .pin8(1'b0), .pin9(C11), .pin10(ALU11), .pin11(U24_pin9), .pin12(U24_pin7), .pin13(ALU10),
    .pin14(U23_pin7), .pin15(U23_pin9), .pin16(1'b1));
  PullUp pullup_18 (.out(diodebackward_58_out));
  PullUp pullup_19 (.out(pullup_19_out));
  DiodeBackward diodebackward_60 (.in(ALU_to_RAM_out), .out(pullup_19_out));
  DiodeBackward diodebackward_61 (.in(Deposit_WR_out), .out(pullup_19_out));
  not not_4 (not_4_out, _74540_1_pin17);
  not not_5 (nWE, _74540_1_pin16);
  nand nand_1 (UP, _74540_1_pin13, _74540_1_pin14);
  nand nand_2 (DN, _74540_1_pin12, _74540_1_pin14);
  _74194 _74194_3 (
    .pin1(nCLR_AC), .pin2(AC7), .pin3(ALU8), .pin4(ALU9), .pin5(ALU10), .pin6(ALU11), .pin7(AC12),
    .pin8(1'b0), .pin9(S0), .pin10(S1), .pin11(CLK), .pin12(AC11), .pin13(AC10), .pin14(AC9), .pin15(AC8),
    .pin16(1'b1));
  PullUp pullup_20 (.out(pullup_20_out));
  DiodeBackward diodebackward_62 (.in(Clear_out), .out(diodebackward_62_out));
  DiodeBackward diodebackward_63 (.in(Examine_RD_out), .out(pullup_20_out));
  PullUp pullup_21 (.out(diodebackward_62_out));
  _74540 _74540_1 (
    .pin1(1'b0), .pin2(diodebackward_62_out), .pin3(pullup_20_out), .pin4(pullup_19_out),
    .pin5(diodebackward_58_out), .pin6(diodebackward_53_out), .pin7(pullup_16_out), .pin8(pullup_15_out),
    .pin9(diodebackward_51_out), .pin10(1'b0), .pin11(_74540_1_pin11), .pin12(_74540_1_pin12),
    .pin13(_74540_1_pin13), .pin14(_74540_1_pin14), .pin15(_74540_1_pin15), .pin16(_74540_1_pin16),
    .pin17(_74540_1_pin17), .pin18(RES), .pin19(1'b0), .pin20(1'b1));
  nand nand_3 (nOE, not_4_out, in_9);
  Seven_Seg_Hex seven_seg_hex_13 (.d({A15, A14, A13, A12}), .dp(1'b0));
  Button #(.activeLow("true")) ALU_to_RAM (.out(ALU_to_RAM_out));
  Button #(.activeLow("true")) Clear (.out(Clear_out));
  Button #(.activeLow("true")) Examine_RD (.out(Examine_RD_out));
  Button #(.activeLow("true")) Deposit_WR (.out(Deposit_WR_out));
  Button #(.activeLow("true")) Dec (.out(Dec_out));
  Button #(.activeLow("true")) Inc (.out(Inc_out));
  Button #(.activeLow("true")) Address (.out(Address_out));
  _74173 _74173_1 (
    .pin1(1'b0), .pin2(1'b0), .pin3(A12), .pin4(A13), .pin5(A14), .pin6(A15), .pin7(CLK_t), .pin8(1'b0),
    .pin9(1'b0), .pin10(1'b0), .pin11(A11), .pin12(A10), .pin13(A9), .pin14(A8), .pin15(1'b0), .pin16(1'b1));
  Seven_Seg_Hex seven_seg_hex_14 (.d({A11, A10, A9, A8}), .dp(1'b0));
  Seven_Seg_Hex seven_seg_hex_15 (.d({A7, A6, A5, A4}), .dp(1'b0));
  Seven_Seg_Hex seven_seg_hex_16 (.d({A3, A2, A1, A0}), .dp(1'b0));
  Button #(.activeLow("true")) C (.out(C_out));
  Button #(.activeLow("true")) _8 (.out(_8_out));
  Button #(.activeLow("true")) _4 (.out(_4_out));
  Button #(.activeLow("true")) _0 (.out(_0_out));
  _74173 _74173_2 (
    .pin1(1'b0), .pin2(1'b0), .pin3(A8), .pin4(A9), .pin5(A10), .pin6(A11), .pin7(CLK_t), .pin8(1'b0),
    .pin9(1'b0), .pin10(1'b0), .pin11(A7), .pin12(A6), .pin13(A5), .pin14(A4), .pin15(1'b0), .pin16(1'b1));
  Button #(.activeLow("true")) D (.out(D_out));
  Button #(.activeLow("true")) _9 (.out(_9_out));
  Button #(.activeLow("true")) _5 (.out(_5_out));
  Button #(.activeLow("true")) _1 (.out(_1_out));
  Seven_Seg_Hex seven_seg_hex_17 (.d({Q15, Q14, Q13, Q12}), .dp(1'b0));
  Seven_Seg_Hex seven_seg_hex_18 (.d({Q11, Q10, Q9, Q8}), .dp(1'b0));
  Button #(.activeLow("true")) E (.out(E_out));
  Button #(.activeLow("true")) A (.out(A_out));
  Button #(.activeLow("true")) _6 (.out(_6_out));
  Button #(.activeLow("true")) _2 (.out(_2_out));
  _74173 _74173_3 (
    .pin1(1'b0), .pin2(1'b0), .pin3(A4), .pin4(A5), .pin5(A6), .pin6(A7), .pin7(CLK_t), .pin8(1'b0),
    .pin9(1'b0), .pin10(1'b0), .pin11(A3), .pin12(A2), .pin13(A1), .pin14(A0), .pin15(1'b0), .pin16(1'b1));
  _74153 U34 (
    .pin1(1'b0), .pin2(BUS15), .pin3(AR3), .pin4(AR2), .pin5(AR1), .pin6(AR0), .pin7(U34_pin7), .pin8(1'b0),
    .pin9(U34_pin9), .pin10(F1), .pin11(F2), .pin12(F3), .pin13(F4), .pin14(AC15), .pin15(AL), .pin16(1'b1));
  _74153 U33 (
    .pin1(1'b0), .pin2(BUS14), .pin3(AR3), .pin4(AR2), .pin5(AR1), .pin6(AR0), .pin7(U33_pin7), .pin8(1'b0),
    .pin9(U33_pin9), .pin10(F1), .pin11(F2), .pin12(F3), .pin13(F4), .pin14(AC14), .pin15(AL), .pin16(1'b1));
  _74153 U32 (
    .pin1(1'b0), .pin2(BUS13), .pin3(AR3), .pin4(AR2), .pin5(AR1), .pin6(AR0), .pin7(U32_pin7), .pin8(1'b0),
    .pin9(U32_pin9), .pin10(F1), .pin11(F2), .pin12(F3), .pin13(F4), .pin14(AC13), .pin15(AL), .pin16(1'b1));
  _74153 U31 (
    .pin1(1'b0), .pin2(BUS12), .pin3(AR3), .pin4(AR2), .pin5(AR1), .pin6(AR0), .pin7(U31_pin7), .pin8(1'b0),
    .pin9(U31_pin9), .pin10(F1), .pin11(F2), .pin12(F3), .pin13(F4), .pin14(AC12), .pin15(AL), .pin16(1'b1));
  Seven_Seg_Hex seven_seg_hex_19 (.d({Q7, Q6, Q5, Q4}), .dp(1'b0));
  Seven_Seg_Hex seven_seg_hex_20 (.d({Q3, Q2, Q1, Q0}), .dp(1'b0));
  Button #(.activeLow("true")) F (.out(F_out));
  Button #(.activeLow("true")) B (.out(B_out));
  Button #(.activeLow("true")) _7 (.out(_7_out));
  Button #(.activeLow("true")) _3 (.out(_3_out));
  _74173 _74173_4 (
    .pin1(1'b0), .pin2(1'b0), .pin3(A0), .pin4(A1), .pin5(A2), .pin6(A3), .pin7(CLK_t), .pin8(1'b0),
    .pin9(1'b0), .pin10(1'b0), .pin11(_74173_4_pin11), .pin12(_74173_4_pin12), .pin13(_74173_4_pin13),
    .pin14(_74173_4_pin14), .pin15(1'b0), .pin16(1'b1));
  Seven_Seg_Hex seven_seg_hex_21 (.d({BUS15, BUS14, BUS13, BUS12}), .dp(1'b0));
  _74283 U27 (
    .pin1(ALU13), .pin2(U32_pin9), .pin3(U32_pin7), .pin4(ALU12), .pin5(U31_pin7), .pin6(U31_pin9),
    .pin7(C11), .pin8(1'b0), .pin9(C15), .pin10(ALU15), .pin11(U34_pin9), .pin12(U34_pin7), .pin13(ALU14),
    .pin14(U33_pin7), .pin15(U33_pin9), .pin16(1'b1));
  Seven_Seg_Hex seven_seg_hex_22 (.d({BUS11, BUS10, BUS9, BUS8}), .dp(1'b0));
  PullUp pullup_22 (.out(pullup_22_out));
  DiodeBackward diodebackward_64 (.in(F_out), .out(pullup_22_out));
  DiodeBackward diodebackward_65 (.in(E_out), .out(pullup_22_out));
  DiodeBackward diodebackward_66 (.in(D_out), .out(pullup_22_out));
  DiodeBackward diodebackward_67 (.in(C_out), .out(pullup_22_out));
  DiodeBackward diodebackward_68 (.in(B_out), .out(pullup_22_out));
  DiodeBackward diodebackward_69 (.in(A_out), .out(pullup_22_out));
  DiodeBackward diodebackward_70 (.in(_9_out), .out(pullup_22_out));
  DiodeBackward diodebackward_71 (.in(_8_out), .out(pullup_22_out));
  not not_6 (_74173_4_pin11, pullup_22_out);
  Seven_Seg_Hex seven_seg_hex_23 (.d({BUS7, BUS6, BUS5, BUS4}), .dp(1'b0));
  PullUp pullup_23 (.out(pullup_23_out));
  DiodeBackward diodebackward_72 (.in(F_out), .out(pullup_23_out));
  DiodeBackward diodebackward_73 (.in(F_out), .out(diodebackward_73_out));
  DiodeBackward diodebackward_74 (.in(E_out), .out(pullup_23_out));
  DiodeBackward diodebackward_75 (.in(E_out), .out(diodebackward_73_out));
  DiodeBackward diodebackward_76 (.in(D_out), .out(pullup_23_out));
  DiodeBackward diodebackward_77 (.in(C_out), .out(pullup_23_out));
  DiodeBackward diodebackward_78 (.in(B_out), .out(diodebackward_73_out));
  DiodeBackward diodebackward_79 (.in(A_out), .out(diodebackward_73_out));
  DiodeBackward diodebackward_80 (.in(_7_out), .out(pullup_23_out));
  DiodeBackward diodebackward_81 (.in(_7_out), .out(diodebackward_73_out));
  DiodeBackward diodebackward_82 (.in(_6_out), .out(pullup_23_out));
  DiodeBackward diodebackward_83 (.in(_6_out), .out(diodebackward_73_out));
  DiodeBackward diodebackward_84 (.in(_5_out), .out(pullup_23_out));
  DiodeBackward diodebackward_85 (.in(_4_out), .out(pullup_23_out));
  DiodeBackward diodebackward_86 (.in(_3_out), .out(diodebackward_73_out));
  DiodeBackward diodebackward_87 (.in(_2_out), .out(diodebackward_73_out));
  not not_7 (_74173_4_pin12, pullup_23_out);
  _74194 _74194_4 (
    .pin1(nCLR_AC), .pin2(AC11), .pin3(ALU12), .pin4(ALU13), .pin5(ALU14), .pin6(ALU15), .pin7(SL),
    .pin8(1'b0), .pin9(S0), .pin10(S1), .pin11(CLK), .pin12(AC15), .pin13(AC14), .pin14(AC13), .pin15(AC12),
    .pin16(1'b1));
  Seven_Seg_Hex seven_seg_hex_24 (.d({BUS3, BUS2, BUS1, BUS0}), .dp(1'b0));
  PullUp pullup_24 (.out(diodebackward_73_out));
  DiodeBackward diodebackward_88 (.in(F_out), .out(diodebackward_88_out));
  DiodeBackward diodebackward_89 (.in(D_out), .out(diodebackward_88_out));
  DiodeBackward diodebackward_90 (.in(B_out), .out(diodebackward_88_out));
  DiodeBackward diodebackward_91 (.in(_9_out), .out(diodebackward_88_out));
  DiodeBackward diodebackward_92 (.in(_7_out), .out(diodebackward_88_out));
  DiodeBackward diodebackward_93 (.in(_5_out), .out(diodebackward_88_out));
  DiodeBackward diodebackward_94 (.in(_3_out), .out(diodebackward_88_out));
  DiodeBackward diodebackward_95 (.in(_1_out), .out(diodebackward_88_out));
  not not_8 (_74173_4_pin13, diodebackward_73_out);
  PullUp pullup_25 (.out(diodebackward_88_out));
  PullUp pullup_26 (.out(pullup_26_out));
  DiodeBackward diodebackward_96 (.in(F_out), .out(pullup_26_out));
  DiodeBackward diodebackward_97 (.in(E_out), .out(pullup_26_out));
  DiodeBackward diodebackward_98 (.in(D_out), .out(pullup_26_out));
  DiodeBackward diodebackward_99 (.in(C_out), .out(pullup_26_out));
  DiodeBackward diodebackward_100 (.in(B_out), .out(pullup_26_out));
  DiodeBackward diodebackward_101 (.in(A_out), .out(pullup_26_out));
  DiodeBackward diodebackward_102 (.in(_9_out), .out(pullup_26_out));
  DiodeBackward diodebackward_103 (.in(_8_out), .out(pullup_26_out));
  DiodeBackward diodebackward_104 (.in(_7_out), .out(pullup_26_out));
  DiodeBackward diodebackward_105 (.in(_6_out), .out(pullup_26_out));
  DiodeBackward diodebackward_106 (.in(_5_out), .out(pullup_26_out));
  DiodeBackward diodebackward_107 (.in(_4_out), .out(pullup_26_out));
  DiodeBackward diodebackward_108 (.in(_3_out), .out(pullup_26_out));
  DiodeBackward diodebackward_109 (.in(_2_out), .out(pullup_26_out));
  DiodeBackward diodebackward_110 (.in(_1_out), .out(pullup_26_out));
  DiodeBackward diodebackward_111 (.in(_0_out), .out(pullup_26_out));
  not not_9 (_74173_4_pin14, diodebackward_88_out);
  not not_10 (not_10_out, pullup_26_out);
  not not_11 (CLK_t, not_10_out);
  LED led_1 (.in(C15));
  _74193 _74193_1 (
    .pin1(A1), .pin2(Q1), .pin3(Q0), .pin4(DN), .pin5(UP), .pin6(Q2), .pin7(Q3), .pin8(1'b0), .pin9(A3),
    .pin10(A2), .pin11(nLD), .pin12(_74193_1_pin12), .pin13(_74193_1_pin13), .pin14(RES), .pin15(A0),
    .pin16(1'b1));
  _74193 _74193_2 (
    .pin1(A5), .pin2(Q5), .pin3(Q4), .pin4(_74193_1_pin13), .pin5(_74193_1_pin12), .pin6(Q6), .pin7(Q7),
    .pin8(1'b0), .pin9(A7), .pin10(A6), .pin11(nLD), .pin12(_74193_2_pin12), .pin13(_74193_2_pin13),
    .pin14(RES), .pin15(A4), .pin16(1'b1));
  _74193 _74193_3 (
    .pin1(A9), .pin2(Q9), .pin3(Q8), .pin4(_74193_2_pin13), .pin5(_74193_2_pin12), .pin6(Q10), .pin7(Q11),
    .pin8(1'b0), .pin9(A11), .pin10(A10), .pin11(nLD), .pin12(_74193_3_pin12), .pin13(_74193_3_pin13),
    .pin14(RES), .pin15(A8), .pin16(1'b1));
  _74193 _74193_4 (
    .pin1(A13), .pin2(Q13), .pin3(Q12), .pin4(_74193_3_pin13), .pin5(_74193_3_pin12), .pin6(Q14), .pin7(Q15),
    .pin8(1'b0), .pin9(A15), .pin10(A14), .pin11(nLD), .pin14(RES), .pin15(A12), .pin16(1'b1));  // open: pin12, pin13
  _62256 _62256_1 (
    .A0(Q0), .A1(Q1), .A2(Q2), .A3(Q3), .A4(Q4), .A5(Q5), .A6(Q6), .A7(Q7), .A8(Q8), .A9(Q9), .A10(Q10),
    .A11(Q11), .A12(Q12), .nCE(1'b0), .nOE(nOE), .nWE(nWE), .D0(BUS8), .D1(BUS9), .D2(BUS10), .D3(BUS11),
    .D4(BUS12), .D5(BUS13), .D6(BUS14), .D7(BUS15), .VCC(1'b1), .GND(1'b0), .A13(Q13), .A14(Q14));
  _74541 _74541_1 (
    .pin1(nDE), .pin2(A15), .pin3(A14), .pin4(A13), .pin5(A12), .pin6(A11), .pin7(A10), .pin8(A9), .pin9(A8),
    .pin10(1'b0), .pin11(BUS8), .pin12(BUS9), .pin13(BUS10), .pin14(BUS11), .pin15(BUS12), .pin16(BUS13),
    .pin17(BUS14), .pin18(BUS15), .pin19(nDE), .pin20(1'b1));
  _62256 _62256_2 (
    .A0(Q0), .A1(Q1), .A2(Q2), .A3(Q3), .A4(Q4), .A5(Q5), .A6(Q6), .A7(Q7), .A8(Q8), .A9(Q9), .A10(Q10),
    .A11(Q11), .A12(Q12), .nCE(1'b0), .nOE(nOE), .nWE(nWE), .D0(BUS0), .D1(BUS1), .D2(BUS2), .D3(BUS3),
    .D4(BUS4), .D5(BUS5), .D6(BUS6), .D7(BUS7), .VCC(1'b1), .GND(1'b0), .A13(Q13), .A14(Q14));
  _74541 _74541_2 (
    .pin1(nDE), .pin2(A7), .pin3(A6), .pin4(A5), .pin5(A4), .pin6(A3), .pin7(A2), .pin8(A1), .pin9(A0),
    .pin10(1'b0), .pin11(BUS0), .pin12(BUS1), .pin13(BUS2), .pin14(BUS3), .pin15(BUS4), .pin16(BUS5),
    .pin17(BUS6), .pin18(BUS7), .pin19(nDE), .pin20(1'b1));
  _74541 U28_2 (
    .pin1(in_8), .pin2(AC7), .pin3(AC6), .pin4(AC5), .pin5(AC4), .pin6(AC3), .pin7(AC2), .pin8(AC1),
    .pin9(AC0), .pin10(1'b0), .pin11(BUS0), .pin12(BUS1), .pin13(BUS2), .pin14(BUS3), .pin15(BUS4),
    .pin16(BUS5), .pin17(BUS6), .pin18(BUS7), .pin19(in_8), .pin20(1'b1));
  _74541 U29 (
    .pin1(in_8), .pin2(AC15), .pin3(AC14), .pin4(AC13), .pin5(AC12), .pin6(AC11), .pin7(AC10), .pin8(AC9),
    .pin9(AC8), .pin10(1'b0), .pin11(BUS8), .pin12(BUS9), .pin13(BUS10), .pin14(BUS11), .pin15(BUS12),
    .pin16(BUS13), .pin17(BUS14), .pin18(BUS15), .pin19(in_8), .pin20(1'b1));
  _74573 _74573_1 (
    .pin1(nALB), .pin2(ALU7), .pin3(ALU6), .pin4(ALU5), .pin5(ALU4), .pin6(ALU3), .pin7(ALU2), .pin8(ALU1),
    .pin9(ALU0), .pin10(1'b0), .pin11(nWE), .pin12(BUS0), .pin13(BUS1), .pin14(BUS2), .pin15(BUS3),
    .pin16(BUS4), .pin17(BUS5), .pin18(BUS6), .pin19(BUS7), .pin20(1'b1));
  _74573 _74573_2 (
    .pin1(nALB), .pin2(ALU15), .pin3(ALU14), .pin4(ALU13), .pin5(ALU12), .pin6(ALU11), .pin7(ALU10),
    .pin8(ALU9), .pin9(ALU8), .pin10(1'b0), .pin11(nWE), .pin12(BUS8), .pin13(BUS9), .pin14(BUS10),
    .pin15(BUS11), .pin16(BUS12), .pin17(BUS13), .pin18(BUS14), .pin19(BUS15), .pin20(1'b1));

  // Other names for the same wires on the sheet: CL_AC = nCLR_AC; CLK1 = CLK; CLK2 = CLK; IR4 = in_6; IR5 = in_3;
  //   IR6 = in_4; IR7 = in_5; nAC = in_8

  // Notes on the sheet:
  //   nCLR_AC: default 1
  //   in_8: default 1
  //   in_9: default 1
  //   ALU-0
  //   MUX3
  //   MUX2
  //   MUX1
  //   MUX0
  //   FFFF / ACC
  //   0000 / ACC
  //   AR0
  //   ADDER
  //   AL
  //   AR0/C0
  //   AR2
  //   AR3
  //   ROL
  //   C0
  //   ROR
  //   S1
  //   S0
  //   LOAD
  //   AND
  //   OR
  //   XOR
  //   ADD
  //   SUB
  //   STORE
  //   JMP
  //   SHL
  //   SHR
  //   INC
  //   DEC
  //   ALU-1
  //   FFFF/ACC
  //   0000/ACC
  //   MUX7
  //   MUX6
  //   MUX5
  //   MUX4
  //   ROL, ROR LOGIC
  //   Select Ain
  //   BUS DATA
  //   INSTRUCTION
  //   0  LOAD
  //   1  AND
  //   2  OR
  //   3  XOR
  //   4  ADD
  //   5  SUB
  //   6  STORE
  //   7  JMP
  //   8  SHL
  //   9  SHR
  //   10  ROL
  //   11  ROR
  //   12  INC
  //   13  DEC
  //   14  ???
  //   15   ???
  //   ACCUMULATOR
  //   ALU-2
  //   ALU OUT
  //   Front Panel
  //   UP
  //   DOWN
  //   ~DE
  //   COUNT
  //   WRITE
  //   READ
  //   RESET
  //   KEY DATA
  //   ALU-3
  //   KEYSWITCH REGISTER
  //   RAM ADDRESS
  //   RAM DATA
  //   Cout
  //   PC and RAM
  //   PROGRAM COUNTER
  //   DATA BUFFER HI
  //   RAM HI
  //   DATA BUFFER LO
  //   RAM LO
  //   AC -> BUS
  //   ALU -> BUS
endmodule
