// Digital circuit 27C1024.dig as structural Verilog
module _27C1024 (
  input  nCE,
  input  nOE,
  input  VPP,
  input  VDD,
  input  GND,
  input  I_O0,
  input  I_O1,
  input  I_O2,
  input  I_O3,
  input  I_O4,
  input  I_O5,
  input  I_O6,
  input  I_O7,
  input  A0,
  input  A1,
  input  A2,
  input  A3,
  input  A4,
  input  A5,
  input  A6,
  input  A7,
  input  A8,
  input  A9,
  input  A10,
  input  A11,
  input  A12,
  input  A13,
  input  A14,
  input  A15,
  input  I_O8,
  input  I_O9,
  input  I_O10,
  input  I_O11,
  input  I_O12,
  input  I_O13,
  input  I_O14,
  input  I_O15,
  input  VSS
);

  wire nor_1_out;
  wire [15:0] ROM1_d;

  PowerSupply powersupply_1 (.VDD(VDD), .GND(GND));
  EEPROM #(.AddrBits(16), .Bits(16)) ROM1 (
    .A({A15, A14, A13, A12, A11, A10, A9, A8, A7, A6, A5, A4, A3, A2, A1, A0}), .CS(~nCE), .WE(~VPP),
    .OE(~nOE), .D(ROM1_d));
  nor nor_1 (nor_1_out, nCE, ~VPP, nOE);  // NOr
  BusSplitter #(.Bits(16)) bussplitter_1 (
    .D(ROM1_d), .OE(nor_1_out), .D0(I_O0), .D1(I_O1), .D2(I_O2), .D3(I_O3), .D4(I_O4), .D5(I_O5), .D6(I_O6),
    .D7(I_O7), .D8(I_O8), .D9(I_O9), .D10(I_O10), .D11(I_O11), .D12(I_O12), .D13(I_O13), .D14(I_O14),
    .D15(I_O15));

  assign VSS = GND;

  // Notes on the sheet:
  //   nCE: pin 2, default 1
  //   nOE: pin 20, default 1
  //   VPP: pin 1, default 1
  //   VDD: pin 40, default 1
  //   GND: pin 11
  //   I_O0: pin 19
  //   I_O1: pin 18
  //   I_O2: pin 17
  //   I_O3: pin 16
  //   I_O4: pin 15
  //   I_O5: pin 14
  //   I_O6: pin 13
  //   I_O7: pin 12
  //   A0: pin 21
  //   A1: pin 22
  //   A2: pin 23
  //   A3: pin 24
  //   A4: pin 25
  //   A5: pin 26
  //   A6: pin 27
  //   A7: pin 28
  //   A8: pin 29
  //   A9: pin 31
  //   A10: pin 32
  //   A11: pin 33
  //   A12: pin 34
  //   A13: pin 35
  //   A14: pin 36
  //   A15: pin 37
  //   I_O8: pin 10
  //   I_O9: pin 9
  //   I_O10: pin 8
  //   I_O11: pin 7
  //   I_O12: pin 6
  //   I_O13: pin 5
  //   I_O14: pin 4
  //   I_O15: pin 3
  //   VSS: pin 30
  //   contents of ROM1 (hex, n*v repeats v):
  //   1a0,fc,2,ec,1d,4fc,69,ca,c2,69,de,ff00,69,ca,61,13f0,101,4fc,82,100,8018,c018,200,
  //   8018,c018,400,8018,c018,800,8018,c018,fc,20,21,22,23,24,25,26,27,28,29,2a,2b,2c,2d,
  //   2e,2f,30,31,32,33,34,35,36,37,38,39,3a,3b,3c,3d,3e,3f,40,41,42,43,44,45,46,47,48,
  //   49,4a,4b,4c,4d,4e,4f,50,51,52,53,54,55,56,57,58,59,5a,5b,5c,5d,5e,5f,60,61,62,63,
  //   64,65,66,67,68,69,6a,6b,6c,6d,6e,fc00,70,71,72,73,74,75,76,77,78,79,7a,7b,7c,7d,7e,
  //   7f,80,81,82,83,84,85,86,87,88,89,8a,8b,8c,8d,8e,8f,90,91,92,93,94,95,96,97,98,99,
  //   9a,9b,9c,9d,9e,9f,a0,a1,a2,a3,a4,a5,a6,a7,a8,a9,aa,ab,ac,ad,ae,af,b0,b1,b2,b3,b4,
  //   b5,b6,b7,b8,b9,ba,bb,bc,bd,be,bf,c0,c1,c2,c3,c4,c5,c6,c7,c8,c9,ca,cb,cc,cd,ce,cf,
  //   d0,d1,d2,d3,d4,d5,d6,d7,d8,d9,da,db,dc,dd,de,df,e0,e1,e2,e3,e4,e5,e6,e7,e8,e9,ea,
  //   eb,ec,ed,ee,ef,f0,f1,f2,f3,f4,f5,f6,f7,f8,f9,fa,fb,fc,fd,fe,ff
endmodule
