// Digital circuit Gigatron_Modified_7.dig as structural Verilog
module Gigatron_Modified_7 (
  input  CLR,
  input  in_2,
  input  in_3,
  input  in_4,
  input  SHR,
  input  SHL,
  input  CLR_2,
  input  in_8,
  input  in_9,
  input  in_10,
  input  SHR_2,
  input  SHL_2,
  input  HOLD_LD,
  input  CLR_3,
  input  nOE,
  input  CK,
  input  in_17,
  input  clk
);

  wire _7425_1_pin6, _7425_2_pin6, A0, A1, A2, A3, A4, A5, A6, A7, A8, A9, A10, A11, A12, A13, A14, A15, AC0,
       AC1, AC2, AC3, AC4, AC5, AC6, AC7, ADD, AL, ALU0, ALU1, ALU2, ALU3, ALU4, ALU5, ALU6, ALU7, AND, AR0,
       AR1, AR2, AR3, BUS0, BUS1, BUS2, BUS3, BUS4, BUS5, BUS6, BUS7, button_7_out, C1, CLK2, CO, D0, D1, D2,
       D3, D4, D5, D6, D7, diodebackward_1_out, diodebackward_5_out, diodebackward_7_out,
       diodebackward_9_out, diodebackward_27_out, EH, EL, IC5_pin2, IC5_pin3, IC5_pin8, IC6_pin2, IC6_pin3,
       IC6_pin8, IC6_pin11, IC7_2_pin7, IC7_2_pin9, IC7_pin2, IC7_pin3, IC7_pin8, IC7_pin11, IC8_2_pin7,
       IC8_2_pin9, IC8_pin1, IC8_pin2, IC8_pin3, IC8_pin8, IC8_pin11, IC9_pin7, IC9_pin9, IC10_pin7,
       IC10_pin9, IC16_pin1, IC19_pin7, IC19_pin9, IC19_pin10, IC19_pin11, IC19_pin12, IC19_pin13,
       IC19_pin14, IC19_pin15, IC20_pin7, IC20_pin9, IC20_pin12, IC20_pin13, IC20_pin14, IC20_pin15,
       IC21_pin11, IC21_pin12, IC21_pin13, IC21_pin14, IC21_pin15, IC21_pin16, IC21_pin17, IC21_pin18,
       IC22_pin7, IC23_2_pin7, IC23_2_pin9, IC23_pin15, IC24_2_pin7, IC24_2_pin9, IC24_pin15, IC25_2_pin7,
       IC25_2_pin9, IC25_pin15, IC26_2_pin7, IC26_2_pin9, IC27_pin15, IC28_2_pin2, IC28_2_pin3, IC28_2_pin4,
       IC28_2_pin5, IC28_2_pin6, IC28_2_pin7, IC28_2_pin8, IC28_2_pin9, IC29_pin2, IC29_pin3, IC29_pin4,
       IC29_pin5, IC29_pin6, IC29_pin7, IC29_pin8, IC29_pin9, IR0, IR1, IR2, IR3, IR4, IR5, IR6, IR7, IX, LD,
       nAE, nBF, nDE, nIE, nJMP, nLD, nOE_t, nOL, not_1_out, not_2_out, not_3_out, not_4_out, not_5_out,
       not_7_out, not_9_out, nPH, nPL, nWE, nXL, nYL, OR, OUT0, OUT1, OUT2, OUT3, OUT4, OUT5, OUT6, OUT7,
       PC0, PC1, PC2, PC3, PC4, PC5, PC6, PC7, PC8, PC9, PC10, PC11, PC12, PC13, PC14, PC15, pullup_6_out,
       pullup_8_out, reset_1_out, ST, SUB, X0, X1, X2, X3, X4, X5, X6, X7, XOR, XOUT0, XOUT1, XOUT2, XOUT3,
       XOUT4, XOUT5, XOUT6, XOUT7, Y0, Y1, Y2, Y3, Y4, Y5, Y6, Y7;
  wire [3:0] IC6_pin9, IC7_pin9, IC12S_2_pin15, IC12S_pin15;

  _62256 _62256_1 (
    .A0(A0), .A1(A1), .A2(A2), .A3(A3), .A4(A4), .A5(A5), .A6(A6), .A7(A7), .A8(A8), .A9(A9), .A10(A10),
    .A11(A11), .A12(A12), .nCE(1'b0), .nOE(nOE_t), .nWE(nWE), .D0(BUS0), .D1(BUS1), .D2(BUS2), .D3(BUS3),
    .D4(BUS4), .D5(BUS5), .D6(BUS6), .D7(BUS7), .VCC(1'b1), .GND(1'b0), .A13(A13), .A14(A14));
  _74157 _74157_1 (
    .pin1(1'b0), .pin2(Y4), .pin3(1'b1), .pin4(A12), .pin5(Y5), .pin6(1'b1), .pin7(A13), .pin8(1'b0),
    .pin9(A14), .pin10(1'b1), .pin11(Y6), .pin12(A15), .pin13(1'b1), .pin14(Y7), .pin15(EH), .pin16(1'b1));
  _74157 _74157_2 (
    .pin1(1'b0), .pin2(Y0), .pin3(1'b1), .pin4(A8), .pin5(Y1), .pin6(1'b1), .pin7(A9), .pin8(1'b0),
    .pin9(A10), .pin10(1'b1), .pin11(Y2), .pin12(A11), .pin13(1'b1), .pin14(Y3), .pin15(EH), .pin16(1'b1));
  _74163 IC27 (
    .pin1(1'b1), .pin2(CLK2), .pin3(ALU0), .pin4(ALU1), .pin5(ALU2), .pin6(ALU3), .pin7(IX), .pin8(1'b0),
    .pin9(nXL), .pin10(1'b1), .pin11(X3), .pin12(X2), .pin13(X1), .pin14(X0), .pin15(IC27_pin15), .pin16(1'b1));
  _74163 IC28 (
    .pin1(1'b1), .pin2(CLK2), .pin3(ALU4), .pin4(ALU5), .pin5(ALU6), .pin6(ALU7), .pin7(IX), .pin8(1'b0),
    .pin9(nXL), .pin10(IC27_pin15), .pin11(X7), .pin12(X6), .pin13(X5), .pin14(X4), .pin16(1'b1));  // open: pin15
  _74157 _74157_3 (
    .pin1(EL), .pin2(X4), .pin3(D4), .pin4(A4), .pin5(X5), .pin6(D5), .pin7(A5), .pin8(1'b0), .pin9(A6),
    .pin10(D6), .pin11(X6), .pin12(A7), .pin13(D7), .pin14(X7), .pin15(1'b0), .pin16(1'b1));
  _74157 _74157_4 (
    .pin1(EL), .pin2(X0), .pin3(D0), .pin4(A0), .pin5(X1), .pin6(D1), .pin7(A1), .pin8(1'b0), .pin9(A2),
    .pin10(D2), .pin11(X2), .pin12(A3), .pin13(D3), .pin14(X3), .pin15(1'b0), .pin16(1'b1));
  not not_1 (not_1_out, nDE);
  not not_2 (not_2_out, nOE_t);
  not not_3 (not_3_out, nAE);
  not not_4 (not_4_out, nIE);
  not not_5 (not_5_out, nOL);
  _74173 _74173_1 (
    .pin1(1'b0), .pin2(1'b0), .pin3(Y3), .pin4(Y2), .pin5(Y1), .pin6(Y0), .pin7(CLK2), .pin8(1'b0),
    .pin9(nYL), .pin10(nYL), .pin11(ALU0), .pin12(ALU1), .pin13(ALU2), .pin14(ALU3), .pin15(1'b0),
    .pin16(1'b1));
  _74173 _74173_2 (
    .pin1(1'b0), .pin2(1'b0), .pin3(Y7), .pin4(Y6), .pin5(Y5), .pin6(Y4), .pin7(CLK2), .pin8(1'b0),
    .pin9(nYL), .pin10(nYL), .pin11(ALU4), .pin12(ALU5), .pin13(ALU6), .pin14(ALU7), .pin15(1'b0),
    .pin16(1'b1));
  Seven_Seg_Hex seven_seg_hex_1 (.d({AC7, AC6, AC5, AC4}), .dp(1'b0));
  LED DATA (.in(not_1_out));
  LED RAM (.in(not_2_out));
  LED ACC (.in(not_3_out));
  LED INPUT (.in(not_4_out));
  LED OUTPUT (.in(not_5_out));
  _74173 _74173_3 (
    .pin1(1'b0), .pin2(1'b0), .pin3(OUT3), .pin4(OUT2), .pin5(OUT1), .pin6(OUT0), .pin7(CLK2), .pin8(1'b0),
    .pin9(nOL), .pin10(nOL), .pin11(ALU0), .pin12(ALU1), .pin13(ALU2), .pin14(ALU3), .pin15(1'b0),
    .pin16(1'b1));
  _74173 _74173_4 (
    .pin1(1'b0), .pin2(1'b0), .pin3(OUT7), .pin4(OUT6), .pin5(OUT5), .pin6(OUT4), .pin7(CLK2), .pin8(1'b0),
    .pin9(nOL), .pin10(nOL), .pin11(ALU4), .pin12(ALU5), .pin13(ALU6), .pin14(ALU7), .pin15(1'b0),
    .pin16(1'b1));
  Seven_Seg_Hex seven_seg_hex_2 (.d({AC3, AC2, AC1, AC0}), .dp(1'b0));
  Delay #(.delayTime(2)) delay_1 (.in(clk), .out(CLK2));
  Reset reset_1 (.out(reset_1_out));
  LED led_1 (.in(XOUT3));
  Seven_Seg_Hex seven_seg_hex_3 (.d({A15, A14, A13, A12}), .dp(1'b0));
  LED led_2 (.in(XOUT2));
  _7474 IC8 (
    .pin1(IC8_pin1), .pin2(IC8_pin2), .pin3(IC8_pin3), .pin4(1'b1), .pin5(IC7_pin9[3]), .pin6(IC8_pin2),
    .pin7(1'b0), .pin8(IC8_pin8), .pin9(IC7_pin9[2]), .pin10(1'b1), .pin11(IC8_pin11), .pin12(IC8_pin8),
    .pin13(IC8_pin1), .pin14(1'b1));
  _74163 IC23 (
    .pin1(reset_1_out), .pin2(clk), .pin3(BUS0), .pin4(BUS1), .pin5(BUS2), .pin6(BUS3), .pin7(1'b1),
    .pin8(1'b0), .pin9(nPL), .pin10(1'b1), .pin11(PC3), .pin12(PC2), .pin13(PC1), .pin14(PC0),
    .pin15(IC23_pin15), .pin16(1'b1));
  _74163 IC24 (
    .pin1(reset_1_out), .pin2(clk), .pin3(BUS4), .pin4(BUS5), .pin5(BUS6), .pin6(BUS7), .pin7(1'b1),
    .pin8(1'b0), .pin9(nPL), .pin10(IC23_pin15), .pin11(PC7), .pin12(PC6), .pin13(PC5), .pin14(PC4),
    .pin15(IC24_pin15), .pin16(1'b1));
  _74163 IC25 (
    .pin1(reset_1_out), .pin2(clk), .pin3(Y0), .pin4(Y1), .pin5(Y2), .pin6(Y3), .pin7(1'b1), .pin8(1'b0),
    .pin9(nPH), .pin10(IC24_pin15), .pin11(PC11), .pin12(PC10), .pin13(PC9), .pin14(PC8), .pin15(IC25_pin15),
    .pin16(1'b1));
  _74163 IC26 (
    .pin1(reset_1_out), .pin2(clk), .pin3(Y4), .pin4(Y5), .pin5(Y6), .pin6(Y7), .pin7(1'b1), .pin8(1'b0),
    .pin9(nPH), .pin10(IC25_pin15), .pin11(PC15), .pin12(PC14), .pin13(PC13), .pin14(PC12), .pin16(1'b1));  // open: pin15
  Seven_Seg_Hex seven_seg_hex_4 (.d({A11, A10, A9, A8}), .dp(1'b0));
  LED led_3 (.in(XOUT1));
  Seven_Seg_Hex seven_seg_hex_5 (.d({A7, A6, A5, A4}), .dp(1'b0));
  LED led_4 (.in(XOUT0));
  Button #(.activeLow("true")) CLEAR (.out(IC8_pin1));
  Seven_Seg_Hex seven_seg_hex_6 (.d({A3, A2, A1, A0}), .dp(1'b0));
  LED led_5 (.in(IC7_pin9[3]));
  _7474 IC7 (
    .pin1(IC8_pin1), .pin2(IC7_pin2), .pin3(IC7_pin3), .pin4(1'b1), .pin5(IC7_pin9[0]), .pin6(IC7_pin2),
    .pin7(1'b0), .pin8(IC7_pin8), .pin9(IC7_pin9[1]), .pin10(1'b1), .pin11(IC7_pin11), .pin12(IC7_pin8),
    .pin13(IC8_pin1), .pin14(1'b1));
  Button button_1 (.out(IC8_pin3));
  Seven_Seg_Hex seven_seg_hex_7 (.d({BUS7, BUS6, BUS5, BUS4}), .dp(1'b0));
  _74540 IC21 (
    .pin1(1'b0), .pin2(LD), .pin3(AND), .pin4(OR), .pin5(XOR), .pin6(ADD), .pin7(SUB), .pin8(ST),
    .pin9(nJMP), .pin10(1'b0), .pin11(IC21_pin11), .pin12(IC21_pin12), .pin13(IC21_pin13),
    .pin14(IC21_pin14), .pin15(IC21_pin15), .pin16(IC21_pin16), .pin17(IC21_pin17), .pin18(IC21_pin18),
    .pin19(1'b0), .pin20(1'b1));
  Seven_Seg_Hex seven_seg_hex_8 (.d({BUS3, BUS2, BUS1, BUS0}), .dp(1'b0));
  LED led_6 (.in(IC7_pin9[2]));
  Button button_2 (.out(IC8_pin11));
  LED led_7 (.in(IC7_pin9[1]));
  Button button_3 (.out(IC7_pin11));
  LED led_8 (.in(IC21_pin18));
  LED led_9 (.in(IC21_pin17));
  LED led_10 (.in(IC21_pin16));
  LED led_11 (.in(IC21_pin15));
  LED led_12 (.in(IC21_pin14));
  LED led_13 (.in(IC21_pin13));
  LED led_14 (.in(IC21_pin12));
  LED led_15 (.in(IC21_pin11));
  LED led_16 (.in(IC7_pin9[0]));
  _7474 IC6 (
    .pin1(IC8_pin1), .pin2(IC6_pin2), .pin3(IC6_pin3), .pin4(1'b1), .pin5(IC6_pin9[3]), .pin6(IC6_pin2),
    .pin7(1'b0), .pin8(IC6_pin8), .pin9(IC6_pin9[2]), .pin10(1'b1), .pin11(IC6_pin11), .pin12(IC6_pin8),
    .pin13(IC8_pin1), .pin14(1'b1));
  Button button_4 (.out(IC7_pin3));
  Seven_Seg_Hex seven_seg_hex_9 (.d({OUT7, OUT6, OUT5, OUT4}), .dp(1'b0));
  LED led_17 (.in(IC6_pin9[3]));
  Button button_5 (.out(IC6_pin3));
  Seven_Seg_Hex seven_seg_hex_10 (.d({OUT3, OUT2, OUT1, OUT0}), .dp(1'b0));
  _27C1024 IC27_2 (
    .nCE(1'b0), .nOE(1'b0), .VPP(1'b1), .VDD(1'b1), .GND(1'b0), .I_O0(IC28_2_pin2), .I_O1(IC28_2_pin3),
    .I_O2(IC28_2_pin4), .I_O3(IC28_2_pin5), .I_O4(IC28_2_pin6), .I_O5(IC28_2_pin7), .I_O6(IC28_2_pin8),
    .I_O7(IC28_2_pin9), .A0(PC0), .A1(PC1), .A2(PC2), .A3(PC3), .A4(PC4), .A5(PC5), .A6(PC6), .A7(PC7),
    .A8(PC8), .A9(PC9), .A10(PC10), .A11(PC11), .A12(PC12), .A13(PC13), .A14(PC14), .A15(PC15),
    .I_O8(IC29_pin2), .I_O9(IC29_pin3), .I_O10(IC29_pin4), .I_O11(IC29_pin5), .I_O12(IC29_pin6),
    .I_O13(IC29_pin7), .I_O14(IC29_pin8), .I_O15(IC29_pin9), .VSS(1'b0));
  LED led_18 (.in(IC6_pin9[2]));
  Button button_6 (.out(IC6_pin11));
  Seven_Seg_Hex seven_seg_hex_11 (.d({PC15, PC14, PC13, PC12}), .dp(1'b0));
  LED led_19 (.in(IC6_pin9[1]));
  Button button_7 (.out(button_7_out));
  Seven_Seg_Hex seven_seg_hex_12 (.d({PC11, PC10, PC9, PC8}), .dp(1'b0));
  _7474 IC5 (
    .pin1(IC8_pin1), .pin2(IC5_pin2), .pin3(IC5_pin3), .pin4(1'b1), .pin5(IC6_pin9[0]), .pin6(IC5_pin2),
    .pin7(1'b0), .pin8(IC5_pin8), .pin9(IC6_pin9[1]), .pin10(1'b1), .pin11(button_7_out), .pin12(IC5_pin8),
    .pin13(IC8_pin1), .pin14(1'b1));
  _74574 IC28_2 (
    .pin1(1'b0), .pin2(IC28_2_pin2), .pin3(IC28_2_pin3), .pin4(IC28_2_pin4), .pin5(IC28_2_pin5),
    .pin6(IC28_2_pin6), .pin7(IC28_2_pin7), .pin8(IC28_2_pin8), .pin9(IC28_2_pin9), .pin10(1'b0),
    .pin11(clk), .pin12(IR7), .pin13(IR6), .pin14(IR5), .pin15(IR4), .pin16(IR3), .pin17(IR2), .pin18(IR1),
    .pin19(IR0), .pin20(1'b1));
  _74574 IC29 (
    .pin1(1'b0), .pin2(IC29_pin2), .pin3(IC29_pin3), .pin4(IC29_pin4), .pin5(IC29_pin5), .pin6(IC29_pin6),
    .pin7(IC29_pin7), .pin8(IC29_pin8), .pin9(IC29_pin9), .pin10(1'b0), .pin11(clk), .pin12(D7), .pin13(D6),
    .pin14(D5), .pin15(D4), .pin16(D3), .pin17(D2), .pin18(D1), .pin19(D0), .pin20(1'b1));
  Seven_Seg_Hex seven_seg_hex_13 (.d({PC7, PC6, PC5, PC4}), .dp(1'b0));
  Seven_Seg_Hex seven_seg_hex_14 (.d(IC7_pin9), .dp(1'b0));
  LED led_20 (.in(IC6_pin9[0]));
  Button button_8 (.out(IC5_pin3));
  Seven_Seg_Hex seven_seg_hex_15 (.d({PC3, PC2, PC1, PC0}), .dp(1'b0));
  Seven_Seg_Hex seven_seg_hex_16 (.d(IC6_pin9), .dp(1'b0));
  Seven_Seg_Hex seven_seg_hex_17 (.d({IR7, IR6, IR5, IR4}), .dp(1'b0));
  Seven_Seg_Hex seven_seg_hex_18 (.d({IR3, IR2, IR1, IR0}), .dp(1'b0));
  _74541 IC30 (
    .pin1(nDE), .pin2(D0), .pin3(D1), .pin4(D2), .pin5(D3), .pin6(D4), .pin7(D5), .pin8(D6), .pin9(D7),
    .pin10(1'b0), .pin11(BUS7), .pin12(BUS6), .pin13(BUS5), .pin14(BUS4), .pin15(BUS3), .pin16(BUS2),
    .pin17(BUS1), .pin18(BUS0), .pin19(nDE), .pin20(1'b1));
  _74173 IC16 (
    .pin1(IC16_pin1), .pin2(IC16_pin1), .pin3(BUS4), .pin4(BUS5), .pin5(BUS6), .pin6(BUS7), .pin7(CK),
    .pin8(1'b0), .pin9(HOLD_LD), .pin10(HOLD_LD), .pin11(IC7_pin9[3]), .pin12(IC7_pin9[2]),
    .pin13(IC7_pin9[1]), .pin14(IC7_pin9[0]), .pin15(CLR_3), .pin16(1'b1));
  _74173 IC15 (
    .pin1(IC16_pin1), .pin2(IC16_pin1), .pin3(BUS0), .pin4(BUS1), .pin5(BUS2), .pin6(BUS3), .pin7(CK),
    .pin8(1'b0), .pin9(HOLD_LD), .pin10(HOLD_LD), .pin11(IC6_pin9[3]), .pin12(IC6_pin9[2]),
    .pin13(IC6_pin9[1]), .pin14(IC6_pin9[0]), .pin15(CLR_3), .pin16(1'b1));
  not not_6 (IC16_pin1, nOE);
  Seven_Seg_Hex seven_seg_hex_19 (.d({D7, D6, D5, D4}), .dp(1'b0));
  Seven_Seg_Hex seven_seg_hex_20 (.d({D3, D2, D1, D0}), .dp(1'b0));
  _74153 IC22 (
    .pin1(nJMP), .pin2(CO), .pin3(1'b0), .pin4(IR4), .pin5(IR3), .pin6(IR2), .pin7(IC22_pin7), .pin8(1'b0),
    .pin10(1'b1), .pin11(1'b1), .pin12(1'b1), .pin13(1'b1), .pin14(AC7), .pin15(1'b1), .pin16(1'b1));  // open: pin9
  _74139 IC21_2 (
    .pin1(1'b0), .pin2(IR0), .pin3(IR1), .pin4(nDE), .pin5(nOE_t), .pin6(nAE), .pin7(nIE), .pin8(1'b0),
    .pin12(nBF), .pin13(IR2), .pin14(IR3), .pin15(IR4), .pin16(1'b1));  // open: pin9, pin10, pin11
  _74138 IC20 (
    .pin1(IR2), .pin2(IR3), .pin3(IR4), .pin4(IR7), .pin5(IR7), .pin6(1'b1), .pin7(IC20_pin7), .pin8(1'b0),
    .pin9(IC20_pin9), .pin10(nYL), .pin11(nXL), .pin12(IC20_pin12), .pin13(IC20_pin13), .pin14(IC20_pin14),
    .pin15(IC20_pin15), .pin16(1'b1));
  _74138 IC18 (
    .pin1(IR5), .pin2(IR6), .pin3(IR7), .pin4(1'b0), .pin5(1'b0), .pin6(1'b1), .pin7(nJMP), .pin8(1'b0),
    .pin9(ST), .pin10(SUB), .pin11(ADD), .pin12(XOR), .pin13(OR), .pin14(AND), .pin15(LD), .pin16(1'b1));
  _74138 IC19 (
    .pin1(IR5), .pin2(IR6), .pin3(IR7), .pin4(1'b0), .pin5(1'b0), .pin6(1'b0), .pin7(IC19_pin7), .pin8(1'b0),
    .pin9(IC19_pin9), .pin10(IC19_pin10), .pin11(IC19_pin11), .pin12(IC19_pin12), .pin13(IC19_pin13),
    .pin14(IC19_pin14), .pin15(IC19_pin15), .pin16(1'b1));
  _74541 _74541_1 (
    .pin1(nAE), .pin2(AC7), .pin3(AC6), .pin4(AC5), .pin5(AC4), .pin6(AC3), .pin7(AC2), .pin8(AC1),
    .pin9(AC0), .pin10(1'b0), .pin11(BUS0), .pin12(BUS1), .pin13(BUS2), .pin14(BUS3), .pin15(BUS4),
    .pin16(BUS5), .pin17(BUS6), .pin18(BUS7), .pin19(nAE), .pin20(1'b1));
  DiodeBackward diodebackward_1 (.in(IC20_pin15), .out(diodebackward_1_out));
  DiodeBackward diodebackward_2 (.in(IC20_pin14), .out(diodebackward_1_out));
  DiodeBackward diodebackward_3 (.in(IC20_pin13), .out(diodebackward_1_out));
  DiodeBackward diodebackward_4 (.in(IC20_pin12), .out(diodebackward_1_out));
  DiodeBackward diodebackward_5 (.in(IR7), .out(diodebackward_5_out));
  DiodeBackward diodebackward_6 (.in(nJMP), .out(diodebackward_5_out));
  not not_7 (not_7_out, IC22_pin7);
  PullUp pullup_1 (.out(diodebackward_1_out));
  DiodeBackward diodebackward_7 (.in(IC20_pin9), .out(diodebackward_7_out));
  DiodeBackward diodebackward_8 (.in(IC20_pin7), .out(diodebackward_7_out));
  PullUp pullup_2 (.out(diodebackward_5_out));
  DiodeBackward diodebackward_9 (.in(LD), .out(diodebackward_9_out));
  DiodeBackward diodebackward_10 (.in(AND), .out(diodebackward_9_out));
  DiodeBackward diodebackward_11 (.in(OR), .out(diodebackward_9_out));
  DiodeBackward diodebackward_12 (.in(ADD), .out(diodebackward_9_out));
  PullUp pullup_3 (.out(diodebackward_7_out));
  PullUp pullup_4 (.out(EL));
  DiodeBackward diodebackward_13 (.in(IC20_pin14), .out(EL));
  DiodeBackward diodebackward_14 (.in(IC20_pin12), .out(EL));
  DiodeBackward diodebackward_15 (.in(IC20_pin7), .out(EL));
  PullUp pullup_5 (.out(diodebackward_9_out));
  PullUp pullup_6 (.out(pullup_6_out));
  DiodeBackward diodebackward_16 (.in(LD), .out(pullup_6_out));
  DiodeBackward diodebackward_17 (.in(OR), .out(pullup_6_out));
  DiodeBackward diodebackward_18 (.in(XOR), .out(pullup_6_out));
  DiodeBackward diodebackward_19 (.in(ADD), .out(pullup_6_out));
  DiodeBackward diodebackward_20 (.in(ST), .out(pullup_6_out));
  or or_1 (nPH, nJMP, nBF);
  PullUp pullup_7 (.out(EH));
  DiodeBackward diodebackward_21 (.in(IC20_pin13), .out(EH));
  DiodeBackward diodebackward_22 (.in(IC20_pin12), .out(EH));
  DiodeBackward diodebackward_23 (.in(IC20_pin7), .out(EH));
  PullUp pullup_8 (.out(pullup_8_out));
  DiodeBackward diodebackward_24 (.in(OR), .out(pullup_8_out));
  DiodeBackward diodebackward_25 (.in(XOR), .out(pullup_8_out));
  DiodeBackward diodebackward_26 (.in(SUB), .out(pullup_8_out));
  DiodeBackward diodebackward_27 (.in(SUB), .out(diodebackward_27_out));
  DiodeBackward diodebackward_28 (.in(ST), .out(diodebackward_27_out));
  _74573 _74573_1 (
    .pin1(in_17), .pin2(AC7), .pin3(AC6), .pin4(AC5), .pin5(AC4), .pin6(AC3), .pin7(AC2), .pin8(AC1),
    .pin9(AC0), .pin10(1'b0), .pin11(OUT6), .pin12(XOUT0), .pin13(XOUT1), .pin14(XOUT2), .pin15(XOUT3),
    .pin16(XOUT4), .pin17(XOUT5), .pin18(XOUT6), .pin19(XOUT7), .pin20(1'b1));
  PullUp pullup_9 (.out(diodebackward_27_out));
  DiodeBackward diodebackward_29 (.in(not_7_out), .out(nPL));
  DiodeBackward diodebackward_30 (.in(nPH), .out(nPL));
  PullUp pullup_10 (.out(nPL));
  not not_8 (IX, IC20_pin7);
  not not_9 (not_9_out, ST);
  _74540 IC20_2 (
    .pin1(1'b0), .pin2(diodebackward_9_out), .pin3(pullup_6_out), .pin4(pullup_8_out),
    .pin5(diodebackward_27_out), .pin6(diodebackward_5_out), .pin7(1'b0), .pin8(1'b0), .pin9(1'b0),
    .pin10(1'b0), .pin14(AL), .pin15(AR0), .pin16(AR1), .pin17(AR2), .pin18(AR3), .pin19(1'b0), .pin20(1'b1));  // open: pin11, pin12, pin13
  or or_2 (nOL, diodebackward_7_out, not_9_out);
  or or_3 (nLD, diodebackward_1_out, not_9_out);
  or or_4 (nWE, clk, ST);
  _74153 IC26_2 (
    .pin1(1'b0), .pin2(BUS7), .pin3(AR3), .pin4(AR2), .pin5(AR1), .pin6(AR0), .pin7(IC26_2_pin7),
    .pin8(1'b0), .pin9(IC26_2_pin9), .pin10(1'b0), .pin11(1'b1), .pin12(1'b0), .pin13(1'b1), .pin14(AC7),
    .pin15(AL), .pin16(1'b1));
  _74153 IC25_2 (
    .pin1(1'b0), .pin2(BUS6), .pin3(AR3), .pin4(AR2), .pin5(AR1), .pin6(AR0), .pin7(IC25_2_pin7),
    .pin8(1'b0), .pin9(IC25_2_pin9), .pin10(1'b0), .pin11(1'b1), .pin12(1'b0), .pin13(1'b1), .pin14(AC6),
    .pin15(AL), .pin16(1'b1));
  _74153 IC24_2 (
    .pin1(1'b0), .pin2(BUS5), .pin3(AR3), .pin4(AR2), .pin5(AR1), .pin6(AR0), .pin7(IC24_2_pin7),
    .pin8(1'b0), .pin9(IC24_2_pin9), .pin10(1'b0), .pin11(1'b1), .pin12(1'b0), .pin13(1'b1), .pin14(AC5),
    .pin15(AL), .pin16(1'b1));
  _74153 IC23_2 (
    .pin1(1'b0), .pin2(BUS4), .pin3(AR3), .pin4(AR2), .pin5(AR1), .pin6(AR0), .pin7(IC23_2_pin7),
    .pin8(1'b0), .pin9(IC23_2_pin9), .pin10(1'b0), .pin11(1'b1), .pin12(1'b0), .pin13(1'b1), .pin14(AC4),
    .pin15(AL), .pin16(1'b1));
  _74153 IC10 (
    .pin1(1'b0), .pin2(BUS3), .pin3(AR3), .pin4(AR2), .pin5(AR1), .pin6(AR0), .pin7(IC10_pin7), .pin8(1'b0),
    .pin9(IC10_pin9), .pin10(1'b0), .pin11(1'b1), .pin12(1'b0), .pin13(1'b1), .pin14(AC3), .pin15(AL),
    .pin16(1'b1));
  _74153 IC9 (
    .pin1(1'b0), .pin2(BUS2), .pin3(AR3), .pin4(AR2), .pin5(AR1), .pin6(AR0), .pin7(IC9_pin7), .pin8(1'b0),
    .pin9(IC9_pin9), .pin10(1'b0), .pin11(1'b1), .pin12(1'b0), .pin13(1'b1), .pin14(AC2), .pin15(AL),
    .pin16(1'b1));
  _74153 IC8_2 (
    .pin1(1'b0), .pin2(BUS1), .pin3(AR3), .pin4(AR2), .pin5(AR1), .pin6(AR0), .pin7(IC8_2_pin7), .pin8(1'b0),
    .pin9(IC8_2_pin9), .pin10(1'b0), .pin11(1'b1), .pin12(1'b0), .pin13(1'b1), .pin14(AC1), .pin15(AL),
    .pin16(1'b1));
  _74153 IC7_2 (
    .pin1(1'b0), .pin2(BUS0), .pin3(AR3), .pin4(AR2), .pin5(AR1), .pin6(AR0), .pin7(IC7_2_pin7), .pin8(1'b0),
    .pin9(IC7_2_pin9), .pin10(1'b0), .pin11(1'b1), .pin12(1'b0), .pin13(1'b1), .pin14(AC0), .pin15(AL),
    .pin16(1'b1));
  _74283 IC12 (
    .pin1(ALU5), .pin2(IC24_2_pin9), .pin3(IC24_2_pin7), .pin4(ALU4), .pin5(IC23_2_pin7), .pin6(IC23_2_pin9),
    .pin7(C1), .pin8(1'b0), .pin9(CO), .pin10(ALU7), .pin11(IC26_2_pin9), .pin12(IC26_2_pin7), .pin13(ALU6),
    .pin14(IC25_2_pin7), .pin15(IC25_2_pin9), .pin16(1'b1));
  _74283 IC11 (
    .pin1(ALU1), .pin2(IC8_2_pin9), .pin3(IC8_2_pin7), .pin4(ALU0), .pin5(IC7_2_pin7), .pin6(IC7_2_pin9),
    .pin7(AR0), .pin8(1'b0), .pin9(C1), .pin10(ALU3), .pin11(IC10_pin9), .pin12(IC10_pin7), .pin13(ALU2),
    .pin14(IC9_pin7), .pin15(IC9_pin9), .pin16(1'b1));
  LED led_21 (.in(CO));
  LED led_22 (.in(C1));
  _74173 IC12A (
    .pin1(in_8), .pin2(in_8), .pin3(AC4), .pin4(AC5), .pin5(AC6), .pin6(AC7), .pin7(CLK2), .pin8(1'b0),
    .pin9(nLD), .pin10(nLD), .pin11(ALU7), .pin12(ALU6), .pin13(ALU5), .pin14(ALU4), .pin15(CLR_2),
    .pin16(1'b1));
  LED led_23 (.in(ALU7));
  LED led_24 (.in(ALU6));
  LED led_25 (.in(ALU3));
  LED led_26 (.in(ALU5));
  LED led_27 (.in(ALU4));
  _74173 IC12A_2 (
    .pin1(in_2), .pin2(in_2), .pin3(AC0), .pin4(AC1), .pin5(AC2), .pin6(AC3), .pin7(CLK2), .pin8(1'b0),
    .pin9(nLD), .pin10(nLD), .pin11(ALU3), .pin12(ALU2), .pin13(ALU1), .pin14(ALU0), .pin15(CLR), .pin16(1'b1));
  LED led_28 (.in(ALU2));
  LED led_29 (.in(ALU1));
  LED ZERO (.in(_7425_1_pin6));
  LED led_30 (.in(ALU0));
  _74194 IC12S (
    .pin1(1'b1), .pin2(in_9), .pin3(ALU4), .pin4(ALU5), .pin5(ALU6), .pin6(ALU7), .pin7(in_10), .pin8(1'b0),
    .pin9(SHL_2), .pin10(SHR_2), .pin11(CLK2), .pin12(IC12S_pin15[3]), .pin13(IC12S_pin15[2]),
    .pin14(IC12S_pin15[1]), .pin15(IC12S_pin15[0]), .pin16(1'b1));
  LED ZERO_2 (.in(_7425_2_pin6));
  _74194 IC12S_2 (
    .pin1(1'b1), .pin2(in_3), .pin3(ALU0), .pin4(ALU1), .pin5(ALU2), .pin6(ALU3), .pin7(in_4), .pin8(1'b0),
    .pin9(SHL), .pin10(SHR), .pin11(CLK2), .pin12(IC12S_2_pin15[3]), .pin13(IC12S_2_pin15[2]),
    .pin14(IC12S_2_pin15[1]), .pin15(IC12S_2_pin15[0]), .pin16(1'b1));
  _7425 _7425_1 (
    .pin1(IC12S_pin15[0]), .pin2(IC12S_pin15[1]), .pin4(IC12S_pin15[2]), .pin5(IC12S_pin15[3]),
    .pin6(_7425_1_pin6), .pin7(1'b0), .pin9(1'b1), .pin10(1'b1), .pin12(1'b1), .pin13(1'b1), .pin14(1'b1));  // open: pin3, pin8, pin11
  Seven_Seg_Hex seven_seg_hex_21 (.d(IC12S_pin15), .dp(1'b0));
  _7425 _7425_2 (
    .pin1(IC12S_2_pin15[0]), .pin2(IC12S_2_pin15[1]), .pin4(IC12S_2_pin15[2]), .pin5(IC12S_2_pin15[3]),
    .pin6(_7425_2_pin6), .pin7(1'b0), .pin9(1'b1), .pin10(1'b1), .pin12(1'b1), .pin13(1'b1), .pin14(1'b1));  // open: pin3, pin8, pin11
  Seven_Seg_Hex seven_seg_hex_22 (.d(IC12S_2_pin15), .dp(1'b0));

  // Other names for the same wires on the sheet: CLK1 = clk

  // Notes on the sheet:
  //   clk: Hz: 10
  //   RAM & X Y REGS
  //   Y SELECT
  //   X REGISTER
  //   32K RAM
  //   X SELECT
  //   PROGRAM COUNTER & ROM
  //   FRONT PANEL SWITCHES
  //   OUTPUT REGISTER
  //   Y REGISTER
  //   ACCUMULATOR
  //   BUS SOURCE
  //   XOUT LEDS
  //   RAM ADDRESS
  //   INSTRUCTION
  //   BUS DATA
  //   ADDRESS
  //   OUTPUT
  //   LOAD
  //   AND
  //   OR
  //   XOR
  //   ADD
  //   SUB
  //   STORE
  //   JMP
  //   DATA
  //   PC ADDRESS
  //   SWITCHES
  //   CONTROL UNIT
  //   AC -> BUS
  //   EXT. OUTPUT
  //   16-bit Jump Detector
  //   INST 8
  //   INST 9
  //   INST A
  //   INST B
  //   INST C
  //   INST D
  //   INST E
  //   INST F
  //   ~W
  //   ALU-H
  //   ALU-L
  //   MUX3
  //   MUX2
  //   MUX1
  //   MUX0
  //   ADDER
  //   Cout
  //   RESULT
endmodule
