// Digital circuit Modified_Gigatron_10.dig as structural Verilog
module Modified_Gigatron_10 (
  input  CLR,
  input  in_2,
  input  in_3,
  input  in_4,
  input  SHR,
  input  SHL,
  input  CLR_2,
  input  in_8,
  input  in_9,
  input  in_10,
  input  SHR_2,
  input  SHL_2,
  input  CK,
  input  in_14,
  input  CLK,
  input  HOLD_LD,
  input  CLR_3,
  input  nOE
);

  wire _7425_1_pin6, _7425_2_pin6, A0, A1, A2, A3, A4, A5, A6, A7, A8, A9, A10, A11, A12, A13, A14, A15, AC0,
       AC1, AC2, AC3, AC4, AC5, AC6, AC7, ADD, AL, ALU0, ALU1, ALU2, ALU3, ALU4, ALU5, ALU6, ALU7, AND, AR0,
       AR1, AR2, AR3, BUS0, BUS1, BUS2, BUS3, BUS4, BUS5, BUS6, BUS7, C1, CLK2, CO, D0, D1, D2, D3, D4, D5,
       D6, D7, diodebackward_1_out, diodebackward_5_out, diodebackward_7_out, diodebackward_9_out,
       diodebackward_27_out, EH, EL, IC5_pin2, IC5_pin3, IC5_pin8, IC5_pin11, IC6_pin2, IC6_pin3, IC6_pin8,
       IC6_pin11, IC7_pin2, IC7_pin3, IC7_pin8, IC7_pin11, IC8_pin1, IC8_pin2, IC8_pin3, IC8_pin8, IC8_pin11,
       IC16_pin1, IC21_pin11, IC21_pin12, IC21_pin13, IC21_pin14, IC21_pin15, IC21_pin16, IC21_pin17,
       IC21_pin18, IR0, IR1, IR2, IR3, IR4, IR5, IR6, IR7, IX, LD, nAE, nBF, nDE, nIE, nJMP, nLD, nOE_t, nOL,
       not_1_out, not_2_out, not_3_out, not_4_out, not_5_out, not_6_out, not_8_out, nPH, nPL, nWE, nXL, nYL,
       OR, OUT0, OUT1, OUT2, OUT3, OUT4, OUT5, OUT6, OUT7, PC0, PC1, PC2, PC3, PC4, PC5, PC6, PC7, PC8, PC9,
       PC10, PC11, PC12, PC13, PC14, PC15, pullup_6_out, pullup_8_out, reset_1_out, ST, SUB, SW0, SW1, SW2,
       SW3, SW4, SW5, SW6, SW7, U3_pin15, U4_pin15, U5_pin15, U8_pin2, U8_pin3, U8_pin4, U8_pin5, U8_pin6,
       U8_pin7, U8_pin8, U8_pin9, U9_pin2, U9_pin3, U9_pin4, U9_pin5, U9_pin6, U9_pin7, U9_pin8, U9_pin9,
       U12_pin7, U13_pin7, U13_pin9, U13_pin12, U13_pin13, U13_pin14, U13_pin15, U17_pin7, U17_pin9,
       U18_pin7, U18_pin9, U19_pin7, U19_pin9, U20_pin7, U20_pin9, U21_pin7, U21_pin9, U22_pin7, U22_pin9,
       U23_pin7, U23_pin9, U24_pin7, U24_pin9, U29_pin15, U35_pin15, X0, X1, X2, X3, X4, X5, X6, X7, XOR,
       XOUT0, XOUT1, XOUT2, XOUT3, XOUT4, XOUT5, XOUT6, XOUT7, Y0, Y1, Y2, Y3, Y4, Y5, Y6, Y7;
  wire [3:0] IC12S_2_pin15, IC12S_pin15;

  _62256 U36 (
    .A0(A0), .A1(A1), .A2(A2), .A3(A3), .A4(A4), .A5(A5), .A6(A6), .A7(A7), .A8(A8), .A9(A9), .A10(A10),
    .A11(A11), .A12(A12), .nCE(1'b0), .nOE(nOE_t), .nWE(nWE), .D0(BUS0), .D1(BUS1), .D2(BUS2), .D3(BUS3),
    .D4(BUS4), .D5(BUS5), .D6(BUS6), .D7(BUS7), .VCC(1'b1), .GND(1'b0), .A13(A13), .A14(A14));
  _74157 U33 (
    .pin1(1'b0), .pin2(Y4), .pin3(1'b1), .pin4(A12), .pin5(Y5), .pin6(1'b1), .pin7(A13), .pin8(1'b0),
    .pin9(A14), .pin10(1'b1), .pin11(Y6), .pin12(A15), .pin13(1'b1), .pin14(Y7), .pin15(EH), .pin16(1'b1));
  _74157 U32 (
    .pin1(1'b0), .pin2(Y0), .pin3(1'b1), .pin4(A8), .pin5(Y1), .pin6(1'b1), .pin7(A9), .pin8(1'b0),
    .pin9(A10), .pin10(1'b1), .pin11(Y2), .pin12(A11), .pin13(1'b1), .pin14(Y3), .pin15(EH), .pin16(1'b1));
  _74163 U29 (
    .pin1(1'b1), .pin2(CLK2), .pin3(ALU0), .pin4(ALU1), .pin5(ALU2), .pin6(ALU3), .pin7(IX), .pin8(1'b0),
    .pin9(nXL), .pin10(1'b1), .pin11(X3), .pin12(X2), .pin13(X1), .pin14(X0), .pin15(U29_pin15), .pin16(1'b1));
  _74163 U30 (
    .pin1(1'b1), .pin2(CLK2), .pin3(ALU4), .pin4(ALU5), .pin5(ALU6), .pin6(ALU7), .pin7(IX), .pin8(1'b0),
    .pin9(nXL), .pin10(U29_pin15), .pin11(X7), .pin12(X6), .pin13(X5), .pin14(X4), .pin16(1'b1));  // open: pin15
  _74157 U35 (
    .pin1(EL), .pin2(X4), .pin3(D4), .pin4(A4), .pin5(X5), .pin6(D5), .pin7(A5), .pin8(1'b0), .pin9(A6),
    .pin10(D6), .pin11(X6), .pin12(A7), .pin13(D7), .pin14(X7), .pin15(U35_pin15), .pin16(1'b1));
  _74157 U34 (
    .pin1(EL), .pin2(X0), .pin3(D0), .pin4(A0), .pin5(X1), .pin6(D1), .pin7(A1), .pin8(1'b0), .pin9(A2),
    .pin10(D2), .pin11(X2), .pin12(A3), .pin13(D3), .pin14(X3), .pin15(U35_pin15), .pin16(1'b1));
  and and_1 (U35_pin15, nWE, nOE_t);
  Seven_Seg_Hex seven_seg_hex_1 (.d({Y7, Y6, Y5, Y4}), .dp(1'b0));
  Seven_Seg_Hex seven_seg_hex_2 (.d({Y3, Y2, Y1, Y0}), .dp(1'b0));
  Seven_Seg_Hex seven_seg_hex_3 (.d({X7, X6, X5, X4}), .dp(1'b0));
  not not_1 (not_1_out, nDE);
  not not_2 (not_2_out, nOE_t);
  not not_3 (not_3_out, nAE);
  not not_4 (not_4_out, nIE);
  not not_5 (not_5_out, nOL);
  _74540 IC21 (
    .pin1(1'b0), .pin2(LD), .pin3(AND), .pin4(OR), .pin5(XOR), .pin6(ADD), .pin7(SUB), .pin8(ST),
    .pin9(nJMP), .pin10(1'b0), .pin11(IC21_pin11), .pin12(IC21_pin12), .pin13(IC21_pin13),
    .pin14(IC21_pin14), .pin15(IC21_pin15), .pin16(IC21_pin16), .pin17(IC21_pin17), .pin18(IC21_pin18),
    .pin19(1'b0), .pin20(1'b1));
  _74173 U31A (
    .pin1(1'b0), .pin2(1'b0), .pin3(Y3), .pin4(Y2), .pin5(Y1), .pin6(Y0), .pin7(CLK2), .pin8(1'b0),
    .pin9(nYL), .pin10(nYL), .pin11(ALU0), .pin12(ALU1), .pin13(ALU2), .pin14(ALU3), .pin15(1'b0),
    .pin16(1'b1));
  _74173 U31B (
    .pin1(1'b0), .pin2(1'b0), .pin3(Y7), .pin4(Y6), .pin5(Y5), .pin6(Y4), .pin7(CLK2), .pin8(1'b0),
    .pin9(nYL), .pin10(nYL), .pin11(ALU4), .pin12(ALU5), .pin13(ALU6), .pin14(ALU7), .pin15(1'b0),
    .pin16(1'b1));
  Seven_Seg_Hex seven_seg_hex_4 (.d({X3, X2, X1, X0}), .dp(1'b0));
  LED DATA (.in(not_1_out));
  LED RAM (.in(not_2_out));
  LED ACC (.in(not_3_out));
  LED INPUT (.in(not_4_out));
  LED OUTPUT (.in(not_5_out));
  Delay delay_1 (.in(CLK), .out(CLK2));
  Seven_Seg_Hex seven_seg_hex_5 (.d({AC7, AC6, AC5, AC4}), .dp(1'b0));
  LED led_1 (.in(IC21_pin18));
  LED led_2 (.in(IC21_pin17));
  LED led_3 (.in(IC21_pin16));
  LED led_4 (.in(IC21_pin15));
  LED led_5 (.in(IC21_pin14));
  LED led_6 (.in(IC21_pin13));
  LED led_7 (.in(IC21_pin12));
  LED led_8 (.in(IC21_pin11));
  Seven_Seg_Hex seven_seg_hex_6 (.d({AC3, AC2, AC1, AC0}), .dp(1'b0));
  Reset reset_1 (.out(reset_1_out));
  LED led_9 (.in(XOUT3));
  Seven_Seg_Hex seven_seg_hex_7 (.d({A15, A14, A13, A12}), .dp(1'b0));
  LED led_10 (.in(XOUT2));
  _74163 U3 (
    .pin1(reset_1_out), .pin2(CLK), .pin3(BUS0), .pin4(BUS1), .pin5(BUS2), .pin6(BUS3), .pin7(1'b1),
    .pin8(1'b0), .pin9(nPL), .pin10(1'b1), .pin11(PC3), .pin12(PC2), .pin13(PC1), .pin14(PC0),
    .pin15(U3_pin15), .pin16(1'b1));
  _74163 U4 (
    .pin1(reset_1_out), .pin2(CLK), .pin3(BUS4), .pin4(BUS5), .pin5(BUS6), .pin6(BUS7), .pin7(1'b1),
    .pin8(1'b0), .pin9(nPL), .pin10(U3_pin15), .pin11(PC7), .pin12(PC6), .pin13(PC5), .pin14(PC4),
    .pin15(U4_pin15), .pin16(1'b1));
  _74163 U5 (
    .pin1(reset_1_out), .pin2(CLK), .pin3(Y0), .pin4(Y1), .pin5(Y2), .pin6(Y3), .pin7(1'b1), .pin8(1'b0),
    .pin9(nPH), .pin10(U4_pin15), .pin11(PC11), .pin12(PC10), .pin13(PC9), .pin14(PC8), .pin15(U5_pin15),
    .pin16(1'b1));
  _74163 U6 (
    .pin1(reset_1_out), .pin2(CLK), .pin3(Y4), .pin4(Y5), .pin5(Y6), .pin6(Y7), .pin7(1'b1), .pin8(1'b0),
    .pin9(nPH), .pin10(U5_pin15), .pin11(PC15), .pin12(PC14), .pin13(PC13), .pin14(PC12), .pin16(1'b1));  // open: pin15
  Seven_Seg_Hex seven_seg_hex_8 (.d({A11, A10, A9, A8}), .dp(1'b0));
  LED led_11 (.in(XOUT1));
  Seven_Seg_Hex seven_seg_hex_9 (.d({A7, A6, A5, A4}), .dp(1'b0));
  LED led_12 (.in(XOUT0));
  Seven_Seg_Hex seven_seg_hex_10 (.d({A3, A2, A1, A0}), .dp(1'b0));
  Seven_Seg_Hex seven_seg_hex_11 (.d({BUS7, BUS6, BUS5, BUS4}), .dp(1'b0));
  _7474 IC8 (
    .pin1(IC8_pin1), .pin2(IC8_pin2), .pin3(IC8_pin3), .pin4(1'b1), .pin5(SW7), .pin6(IC8_pin2), .pin7(1'b0),
    .pin8(IC8_pin8), .pin9(SW6), .pin10(1'b1), .pin11(IC8_pin11), .pin12(IC8_pin8), .pin13(IC8_pin1),
    .pin14(1'b1));
  Seven_Seg_Hex seven_seg_hex_12 (.d({BUS3, BUS2, BUS1, BUS0}), .dp(1'b0));
  Button #(.activeLow("true")) CLEAR (.out(IC8_pin1));
  _7474 IC7 (
    .pin1(IC8_pin1), .pin2(IC7_pin2), .pin3(IC7_pin3), .pin4(1'b1), .pin5(SW4), .pin6(IC7_pin2), .pin7(1'b0),
    .pin8(IC7_pin8), .pin9(SW5), .pin10(1'b1), .pin11(IC7_pin11), .pin12(IC7_pin8), .pin13(IC8_pin1),
    .pin14(1'b1));
  Seven_Seg_Hex seven_seg_hex_13 (.d({OUT7, OUT6, OUT5, OUT4}), .dp(1'b0));
  LED led_13 (.in(SW7));
  Button button_1 (.out(IC8_pin3));
  Seven_Seg_Hex seven_seg_hex_14 (.d({OUT3, OUT2, OUT1, OUT0}), .dp(1'b0));
  LED led_14 (.in(SW6));
  Button button_2 (.out(IC8_pin11));
  _27C1024 U7 (
    .nCE(1'b0), .nOE(1'b0), .VPP(1'b1), .VDD(1'b1), .GND(1'b0), .I_O0(U8_pin2), .I_O1(U8_pin3),
    .I_O2(U8_pin4), .I_O3(U8_pin5), .I_O4(U8_pin6), .I_O5(U8_pin7), .I_O6(U8_pin8), .I_O7(U8_pin9), .A0(PC0),
    .A1(PC1), .A2(PC2), .A3(PC3), .A4(PC4), .A5(PC5), .A6(PC6), .A7(PC7), .A8(PC8), .A9(PC9), .A10(PC10),
    .A11(PC11), .A12(PC12), .A13(PC13), .A14(PC14), .A15(PC15), .I_O8(U9_pin2), .I_O9(U9_pin3),
    .I_O10(U9_pin4), .I_O11(U9_pin5), .I_O12(U9_pin6), .I_O13(U9_pin7), .I_O14(U9_pin8), .I_O15(U9_pin9),
    .VSS(1'b0));
  Seven_Seg_Hex seven_seg_hex_15 (.d({PC15, PC14, PC13, PC12}), .dp(1'b0));
  LED led_15 (.in(SW5));
  Button button_3 (.out(IC7_pin11));
  Seven_Seg_Hex seven_seg_hex_16 (.d({PC11, PC10, PC9, PC8}), .dp(1'b0));
  LED led_16 (.in(SW4));
  Button button_4 (.out(IC7_pin3));
  _74574 U8 (
    .pin1(1'b0), .pin2(U8_pin2), .pin3(U8_pin3), .pin4(U8_pin4), .pin5(U8_pin5), .pin6(U8_pin6),
    .pin7(U8_pin7), .pin8(U8_pin8), .pin9(U8_pin9), .pin10(1'b0), .pin11(CLK), .pin12(IR7), .pin13(IR6),
    .pin14(IR5), .pin15(IR4), .pin16(IR3), .pin17(IR2), .pin18(IR1), .pin19(IR0), .pin20(1'b1));
  _74574 U9 (
    .pin1(1'b0), .pin2(U9_pin2), .pin3(U9_pin3), .pin4(U9_pin4), .pin5(U9_pin5), .pin6(U9_pin6),
    .pin7(U9_pin7), .pin8(U9_pin8), .pin9(U9_pin9), .pin10(1'b0), .pin11(CLK), .pin12(D7), .pin13(D6),
    .pin14(D5), .pin15(D4), .pin16(D3), .pin17(D2), .pin18(D1), .pin19(D0), .pin20(1'b1));
  Seven_Seg_Hex seven_seg_hex_17 (.d({PC7, PC6, PC5, PC4}), .dp(1'b0));
  _7474 IC6 (
    .pin1(IC8_pin1), .pin2(IC6_pin2), .pin3(IC6_pin3), .pin4(1'b1), .pin5(SW3), .pin6(IC6_pin2), .pin7(1'b0),
    .pin8(IC6_pin8), .pin9(SW2), .pin10(1'b1), .pin11(IC6_pin11), .pin12(IC6_pin8), .pin13(IC8_pin1),
    .pin14(1'b1));
  Seven_Seg_Hex seven_seg_hex_18 (.d({PC3, PC2, PC1, PC0}), .dp(1'b0));
  LED led_17 (.in(SW3));
  Button button_5 (.out(IC6_pin3));
  LED led_18 (.in(SW2));
  Button button_6 (.out(IC6_pin11));
  Seven_Seg_Hex seven_seg_hex_19 (.d({IR7, IR6, IR5, IR4}), .dp(1'b0));
  LED led_19 (.in(SW1));
  _7474 IC5 (
    .pin1(IC8_pin1), .pin2(IC5_pin2), .pin3(IC5_pin3), .pin4(1'b1), .pin5(SW0), .pin6(IC5_pin2), .pin7(1'b0),
    .pin8(IC5_pin8), .pin9(SW1), .pin10(1'b1), .pin11(IC5_pin11), .pin12(IC5_pin8), .pin13(IC8_pin1),
    .pin14(1'b1));
  Button button_7 (.out(IC5_pin11));
  Seven_Seg_Hex seven_seg_hex_20 (.d({IR3, IR2, IR1, IR0}), .dp(1'b0));
  Seven_Seg_Hex seven_seg_hex_21 (.d({SW7, SW6, SW5, SW4}), .dp(1'b0));
  LED led_20 (.in(SW0));
  Button button_8 (.out(IC5_pin3));
  Seven_Seg_Hex seven_seg_hex_22 (.d({SW3, SW2, SW1, SW0}), .dp(1'b0));
  _74541 U10 (
    .pin1(nDE), .pin2(D0), .pin3(D1), .pin4(D2), .pin5(D3), .pin6(D4), .pin7(D5), .pin8(D6), .pin9(D7),
    .pin10(1'b0), .pin11(BUS7), .pin12(BUS6), .pin13(BUS5), .pin14(BUS4), .pin15(BUS3), .pin16(BUS2),
    .pin17(BUS1), .pin18(BUS0), .pin19(nDE), .pin20(1'b1));
  Seven_Seg_Hex seven_seg_hex_23 (.d({D7, D6, D5, D4}), .dp(1'b0));
  Seven_Seg_Hex seven_seg_hex_24 (.d({D3, D2, D1, D0}), .dp(1'b0));
  _74139 U11 (
    .pin1(1'b0), .pin2(IR0), .pin3(IR1), .pin4(nDE), .pin5(nOE_t), .pin6(nAE), .pin7(nIE), .pin8(1'b0),
    .pin12(nBF), .pin13(IR2), .pin14(IR3), .pin15(IR4), .pin16(1'b1));  // open: pin9, pin10, pin11
  _74138 U13 (
    .pin1(IR2), .pin2(IR3), .pin3(IR4), .pin4(1'b0), .pin5(1'b0), .pin6(nJMP), .pin7(U13_pin7), .pin8(1'b0),
    .pin9(U13_pin9), .pin10(nYL), .pin11(nXL), .pin12(U13_pin12), .pin13(U13_pin13), .pin14(U13_pin14),
    .pin15(U13_pin15), .pin16(1'b1));
  _74138 U14 (
    .pin1(IR5), .pin2(IR6), .pin3(IR7), .pin4(1'b0), .pin5(1'b0), .pin6(1'b1), .pin7(nJMP), .pin8(1'b0),
    .pin9(ST), .pin10(SUB), .pin11(ADD), .pin12(XOR), .pin13(OR), .pin14(AND), .pin15(LD), .pin16(1'b1));
  _74173 U37B (
    .pin1(1'b0), .pin2(1'b0), .pin3(OUT7), .pin4(OUT6), .pin5(OUT5), .pin6(OUT4), .pin7(CLK2), .pin8(1'b0),
    .pin9(nOL), .pin10(nOL), .pin11(ALU4), .pin12(ALU5), .pin13(ALU6), .pin14(ALU7), .pin15(1'b0),
    .pin16(1'b1));
  _74173 U37A (
    .pin1(1'b0), .pin2(1'b0), .pin3(OUT3), .pin4(OUT2), .pin5(OUT1), .pin6(OUT0), .pin7(CLK2), .pin8(1'b0),
    .pin9(nOL), .pin10(nOL), .pin11(ALU0), .pin12(ALU1), .pin13(ALU2), .pin14(ALU3), .pin15(1'b0),
    .pin16(1'b1));
  _74541 U28 (
    .pin1(nAE), .pin2(AC7), .pin3(AC6), .pin4(AC5), .pin5(AC4), .pin6(AC3), .pin7(AC2), .pin8(AC1),
    .pin9(AC0), .pin10(1'b0), .pin11(BUS0), .pin12(BUS1), .pin13(BUS2), .pin14(BUS3), .pin15(BUS4),
    .pin16(BUS5), .pin17(BUS6), .pin18(BUS7), .pin19(nAE), .pin20(1'b1));
  DiodeBackward diodebackward_1 (.in(U13_pin15), .out(diodebackward_1_out));
  DiodeBackward diodebackward_2 (.in(U13_pin14), .out(diodebackward_1_out));
  DiodeBackward diodebackward_3 (.in(U13_pin13), .out(diodebackward_1_out));
  DiodeBackward diodebackward_4 (.in(U13_pin12), .out(diodebackward_1_out));
  DiodeBackward diodebackward_5 (.in(IR7), .out(diodebackward_5_out));
  DiodeBackward diodebackward_6 (.in(nJMP), .out(diodebackward_5_out));
  PullUp pullup_1 (.out(diodebackward_1_out));
  DiodeBackward diodebackward_7 (.in(U13_pin9), .out(diodebackward_7_out));
  DiodeBackward diodebackward_8 (.in(U13_pin7), .out(diodebackward_7_out));
  PullUp pullup_2 (.out(diodebackward_5_out));
  DiodeBackward diodebackward_9 (.in(LD), .out(diodebackward_9_out));
  DiodeBackward diodebackward_10 (.in(AND), .out(diodebackward_9_out));
  DiodeBackward diodebackward_11 (.in(OR), .out(diodebackward_9_out));
  DiodeBackward diodebackward_12 (.in(ADD), .out(diodebackward_9_out));
  PullUp pullup_3 (.out(diodebackward_7_out));
  PullUp pullup_4 (.out(EL));
  DiodeBackward diodebackward_13 (.in(U13_pin14), .out(EL));
  DiodeBackward diodebackward_14 (.in(U13_pin12), .out(EL));
  DiodeBackward diodebackward_15 (.in(U13_pin7), .out(EL));
  PullUp pullup_5 (.out(diodebackward_9_out));
  PullUp pullup_6 (.out(pullup_6_out));
  DiodeBackward diodebackward_16 (.in(LD), .out(pullup_6_out));
  DiodeBackward diodebackward_17 (.in(OR), .out(pullup_6_out));
  DiodeBackward diodebackward_18 (.in(XOR), .out(pullup_6_out));
  DiodeBackward diodebackward_19 (.in(ADD), .out(pullup_6_out));
  DiodeBackward diodebackward_20 (.in(ST), .out(pullup_6_out));
  PullUp pullup_7 (.out(EH));
  DiodeBackward diodebackward_21 (.in(U13_pin13), .out(EH));
  DiodeBackward diodebackward_22 (.in(U13_pin12), .out(EH));
  DiodeBackward diodebackward_23 (.in(U13_pin7), .out(EH));
  PullUp pullup_8 (.out(pullup_8_out));
  DiodeBackward diodebackward_24 (.in(OR), .out(pullup_8_out));
  DiodeBackward diodebackward_25 (.in(XOR), .out(pullup_8_out));
  DiodeBackward diodebackward_26 (.in(SUB), .out(pullup_8_out));
  DiodeBackward diodebackward_27 (.in(SUB), .out(diodebackward_27_out));
  DiodeBackward diodebackward_28 (.in(ST), .out(diodebackward_27_out));
  PullUp pullup_9 (.out(diodebackward_27_out));
  _74153 U12 (
    .pin1(nJMP), .pin2(CO), .pin3(1'b0), .pin4(IR4), .pin5(IR3), .pin6(IR2), .pin7(U12_pin7), .pin8(1'b0),
    .pin10(1'b1), .pin11(1'b1), .pin12(1'b1), .pin13(1'b1), .pin14(AC7), .pin15(1'b1), .pin16(1'b1));  // open: pin9
  _74573 U38 (
    .pin1(in_14), .pin2(AC7), .pin3(AC6), .pin4(AC5), .pin5(AC4), .pin6(AC3), .pin7(AC2), .pin8(AC1),
    .pin9(AC0), .pin10(1'b0), .pin11(OUT6), .pin12(XOUT0), .pin13(XOUT1), .pin14(XOUT2), .pin15(XOUT3),
    .pin16(XOUT4), .pin17(XOUT5), .pin18(XOUT6), .pin19(XOUT7), .pin20(1'b1));
  not not_6 (not_6_out, U12_pin7);
  not not_7 (IX, U13_pin7);
  not not_8 (not_8_out, ST);
  _74540 U15 (
    .pin1(1'b0), .pin2(diodebackward_9_out), .pin3(pullup_6_out), .pin4(pullup_8_out),
    .pin5(diodebackward_27_out), .pin6(diodebackward_5_out), .pin7(1'b0), .pin8(1'b0), .pin9(1'b0),
    .pin10(1'b0), .pin14(AL), .pin15(AR0), .pin16(AR1), .pin17(AR2), .pin18(AR3), .pin19(1'b0), .pin20(1'b1));  // open: pin11, pin12, pin13
  _74173 IC16 (
    .pin1(IC16_pin1), .pin2(IC16_pin1), .pin3(BUS4), .pin4(BUS5), .pin5(BUS6), .pin6(BUS7), .pin7(CK),
    .pin8(1'b0), .pin9(HOLD_LD), .pin10(HOLD_LD), .pin11(SW7), .pin12(SW6), .pin13(SW5), .pin14(SW4),
    .pin15(CLR_3), .pin16(1'b1));
  _74173 IC15 (
    .pin1(IC16_pin1), .pin2(IC16_pin1), .pin3(BUS0), .pin4(BUS1), .pin5(BUS2), .pin6(BUS3), .pin7(CK),
    .pin8(1'b0), .pin9(HOLD_LD), .pin10(HOLD_LD), .pin11(SW3), .pin12(SW2), .pin13(SW1), .pin14(SW0),
    .pin15(CLR_3), .pin16(1'b1));
  DiodeBackward diodebackward_29 (.in(not_6_out), .out(nPL));
  DiodeBackward diodebackward_30 (.in(nPH), .out(nPL));
  or or_1 (nOL, diodebackward_7_out, not_8_out);
  or or_2 (nLD, diodebackward_1_out, not_8_out);
  or or_3 (nWE, CLK, ST);
  or or_4 (nPH, nBF, nJMP);
  PullUp pullup_10 (.out(nPL));
  not not_9 (IC16_pin1, nOE);
  _74153 U20 (
    .pin1(1'b0), .pin2(BUS7), .pin3(AR3), .pin4(AR2), .pin5(AR1), .pin6(AR0), .pin7(U20_pin7), .pin8(1'b0),
    .pin9(U20_pin9), .pin10(1'b0), .pin11(1'b1), .pin12(1'b0), .pin13(1'b1), .pin14(AC7), .pin15(AL),
    .pin16(1'b1));
  _74153 U19 (
    .pin1(1'b0), .pin2(BUS6), .pin3(AR3), .pin4(AR2), .pin5(AR1), .pin6(AR0), .pin7(U19_pin7), .pin8(1'b0),
    .pin9(U19_pin9), .pin10(1'b0), .pin11(1'b1), .pin12(1'b0), .pin13(1'b1), .pin14(AC6), .pin15(AL),
    .pin16(1'b1));
  _74153 U18 (
    .pin1(1'b0), .pin2(BUS5), .pin3(AR3), .pin4(AR2), .pin5(AR1), .pin6(AR0), .pin7(U18_pin7), .pin8(1'b0),
    .pin9(U18_pin9), .pin10(1'b0), .pin11(1'b1), .pin12(1'b0), .pin13(1'b1), .pin14(AC5), .pin15(AL),
    .pin16(1'b1));
  _74153 U17 (
    .pin1(1'b0), .pin2(BUS4), .pin3(AR3), .pin4(AR2), .pin5(AR1), .pin6(AR0), .pin7(U17_pin7), .pin8(1'b0),
    .pin9(U17_pin9), .pin10(1'b0), .pin11(1'b1), .pin12(1'b0), .pin13(1'b1), .pin14(AC4), .pin15(AL),
    .pin16(1'b1));
  _74153 U24 (
    .pin1(1'b0), .pin2(BUS3), .pin3(AR3), .pin4(AR2), .pin5(AR1), .pin6(AR0), .pin7(U24_pin7), .pin8(1'b0),
    .pin9(U24_pin9), .pin10(1'b0), .pin11(1'b1), .pin12(1'b0), .pin13(1'b1), .pin14(AC3), .pin15(AL),
    .pin16(1'b1));
  _74153 U23 (
    .pin1(1'b0), .pin2(BUS2), .pin3(AR3), .pin4(AR2), .pin5(AR1), .pin6(AR0), .pin7(U23_pin7), .pin8(1'b0),
    .pin9(U23_pin9), .pin10(1'b0), .pin11(1'b1), .pin12(1'b0), .pin13(1'b1), .pin14(AC2), .pin15(AL),
    .pin16(1'b1));
  _74153 U22 (
    .pin1(1'b0), .pin2(BUS1), .pin3(AR3), .pin4(AR2), .pin5(AR1), .pin6(AR0), .pin7(U22_pin7), .pin8(1'b0),
    .pin9(U22_pin9), .pin10(1'b0), .pin11(1'b1), .pin12(1'b0), .pin13(1'b1), .pin14(AC1), .pin15(AL),
    .pin16(1'b1));
  _74153 U21 (
    .pin1(1'b0), .pin2(BUS0), .pin3(AR3), .pin4(AR2), .pin5(AR1), .pin6(AR0), .pin7(U21_pin7), .pin8(1'b0),
    .pin9(U21_pin9), .pin10(1'b0), .pin11(1'b1), .pin12(1'b0), .pin13(1'b1), .pin14(AC0), .pin15(AL),
    .pin16(1'b1));
  _74283 U25 (
    .pin1(ALU5), .pin2(U18_pin9), .pin3(U18_pin7), .pin4(ALU4), .pin5(U17_pin7), .pin6(U17_pin9), .pin7(C1),
    .pin8(1'b0), .pin9(CO), .pin10(ALU7), .pin11(U20_pin9), .pin12(U20_pin7), .pin13(ALU6), .pin14(U19_pin7),
    .pin15(U19_pin9), .pin16(1'b1));
  _74283 U26 (
    .pin1(ALU1), .pin2(U22_pin9), .pin3(U22_pin7), .pin4(ALU0), .pin5(U21_pin7), .pin6(U21_pin9), .pin7(AR0),
    .pin8(1'b0), .pin9(C1), .pin10(ALU3), .pin11(U24_pin9), .pin12(U24_pin7), .pin13(ALU2), .pin14(U23_pin7),
    .pin15(U23_pin9), .pin16(1'b1));
  LED led_21 (.in(CO));
  LED led_22 (.in(C1));
  _74173 U27B (
    .pin1(in_8), .pin2(in_8), .pin3(AC4), .pin4(AC5), .pin5(AC6), .pin6(AC7), .pin7(CLK2), .pin8(1'b0),
    .pin9(nLD), .pin10(nLD), .pin11(ALU7), .pin12(ALU6), .pin13(ALU5), .pin14(ALU4), .pin15(CLR_2),
    .pin16(1'b1));
  _74173 U27A (
    .pin1(in_2), .pin2(in_2), .pin3(AC0), .pin4(AC1), .pin5(AC2), .pin6(AC3), .pin7(CLK2), .pin8(1'b0),
    .pin9(nLD), .pin10(nLD), .pin11(ALU3), .pin12(ALU2), .pin13(ALU1), .pin14(ALU0), .pin15(CLR), .pin16(1'b1));
  LED ZERO (.in(_7425_1_pin6));
  LED ZERO_2 (.in(_7425_2_pin6));
  _74194 IC12S (
    .pin1(1'b1), .pin2(in_9), .pin3(ALU4), .pin4(ALU5), .pin5(ALU6), .pin6(ALU7), .pin7(in_10), .pin8(1'b0),
    .pin9(SHL_2), .pin10(SHR_2), .pin11(CLK2), .pin12(IC12S_pin15[3]), .pin13(IC12S_pin15[2]),
    .pin14(IC12S_pin15[1]), .pin15(IC12S_pin15[0]), .pin16(1'b1));
  _74194 IC12S_2 (
    .pin1(1'b1), .pin2(in_3), .pin3(ALU0), .pin4(ALU1), .pin5(ALU2), .pin6(ALU3), .pin7(in_4), .pin8(1'b0),
    .pin9(SHL), .pin10(SHR), .pin11(CLK2), .pin12(IC12S_2_pin15[3]), .pin13(IC12S_2_pin15[2]),
    .pin14(IC12S_2_pin15[1]), .pin15(IC12S_2_pin15[0]), .pin16(1'b1));
  _7425 _7425_1 (
    .pin1(IC12S_pin15[0]), .pin2(IC12S_pin15[1]), .pin4(IC12S_pin15[2]), .pin5(IC12S_pin15[3]),
    .pin6(_7425_1_pin6), .pin7(1'b0), .pin9(1'b1), .pin10(1'b1), .pin12(1'b1), .pin13(1'b1), .pin14(1'b1));  // open: pin3, pin8, pin11
  Seven_Seg_Hex seven_seg_hex_25 (.d(IC12S_pin15), .dp(1'b0));
  _7425 _7425_2 (
    .pin1(IC12S_2_pin15[0]), .pin2(IC12S_2_pin15[1]), .pin4(IC12S_2_pin15[2]), .pin5(IC12S_2_pin15[3]),
    .pin6(_7425_2_pin6), .pin7(1'b0), .pin9(1'b1), .pin10(1'b1), .pin12(1'b1), .pin13(1'b1), .pin14(1'b1));  // open: pin3, pin8, pin11
  Seven_Seg_Hex seven_seg_hex_26 (.d(IC12S_2_pin15), .dp(1'b0));

  // Other names for the same wires on the sheet: CLK1 = CLK

  // Notes on the sheet:
  //   RAM & X Y REGS
  //   Y SELECT
  //   X REGISTER
  //   32K RAM
  //   X SELECT
  //   PROGRAM COUNTER & ROM
  //   FRONT PANEL SWITCHES
  //   Y REG
  //   Y REGISTER
  //   BUS SOURCE
  //   INSTRUCTION
  //   X REG
  //   LOAD
  //   AND
  //   OR
  //   XOR
  //   ADD
  //   SUB
  //   STORE
  //   JMP
  //   ACC
  //   XOUT LEDS
  //   RAM ADDRESS
  //   BUS DATA
  //   OUTPUT
  //   ADDRESS
  //   PC ADDRESS
  //   DATA
  //   SWITCHES
  //   CONTROL UNIT
  //   REGISTERS
  //   16-bit Jump Detector
  //   OUTPUT REGISTER
  //   AC -> BUS
  //   SWITCH REGISTER
  //   EXT. OUTPUT
  //   ~W
  //   U16
  //   ALU-H
  //   ALU-L
  //   MUX7
  //   MUX6
  //   MUX5
  //   MUX4
  //   MUX3
  //   MUX2
  //   MUX1
  //   MUX0
  //   ACCUMULATOR
  //   ADDER
  //   Cout
  //   RESULT
endmodule
