// Digital circuit front_panel_2.dig as structural Verilog
module front_panel_2 (
);

  wire _0_out, _1_out, _2_out, _3_out, _4_out, _5_out, _6_out, _7_out, _8_out, _9_out, _74173_4_pin11,
       _74173_4_pin12, _74173_4_pin13, _74173_4_pin14, _74193_1_pin12, _74193_1_pin13, _74193_2_pin12,
       _74193_2_pin13, _74193_3_pin12, _74193_3_pin13, _74540_1_pin11, _74540_1_pin12, _74540_1_pin13,
       _74540_1_pin14, _74540_1_pin15, _74540_1_pin16, _74540_1_pin17, A0, A1, A2, A3, A4, A5, A6, A7, A8,
       A9, A10, A11, A12, A13, A14, A15, A_out, Address_out, B0, B1, B2, B3, B4, B5, B6, B7, B8, B9, B10,
       B11, B12, B13, B14, B15, B_out, C_out, Clear_out, CLK, D_out, Dec_out, Deposit_WR_out,
       diodebackward_1_out, diodebackward_3_out, diodebackward_11_out, diodebackward_14_out,
       diodebackward_25_out, diodebackward_40_out, DN, E_out, Examine_RD_out, F_out, Inc_out, nCE, nDE, nLD,
       nOE, not_9_out, pullup_2_out, pullup_3_out, pullup_6_out, pullup_7_out, pullup_9_out, pullup_10_out,
       pullup_13_out, Q0, Q1, Q2, Q3, Q4, Q5, Q6, Q7, Q8, Q9, Q10, Q11, Q12, Q13, Q14, Q15, RES, UP;

  DiodeBackward diodebackward_1 (.in(Address_out), .out(diodebackward_1_out));
  PullUp pullup_1 (.out(diodebackward_1_out));
  PullUp pullup_2 (.out(pullup_2_out));
  DiodeBackward diodebackward_2 (.in(Dec_out), .out(pullup_2_out));
  not not_1 (nLD, _74540_1_pin11);
  PullUp pullup_3 (.out(pullup_3_out));
  DiodeBackward diodebackward_3 (.in(Examine_RD_out), .out(diodebackward_3_out));
  DiodeBackward diodebackward_4 (.in(Examine_RD_out), .out(pullup_3_out));
  DiodeBackward diodebackward_5 (.in(Deposit_WR_out), .out(diodebackward_3_out));
  DiodeBackward diodebackward_6 (.in(Deposit_WR_out), .out(pullup_3_out));
  DiodeBackward diodebackward_7 (.in(Dec_out), .out(diodebackward_3_out));
  DiodeBackward diodebackward_8 (.in(Inc_out), .out(pullup_3_out));
  DiodeBackward diodebackward_9 (.in(Inc_out), .out(diodebackward_3_out));
  DiodeBackward diodebackward_10 (.in(Address_out), .out(pullup_3_out));
  PullUp pullup_4 (.out(diodebackward_3_out));
  DiodeBackward diodebackward_11 (.in(Examine_RD_out), .out(diodebackward_11_out));
  DiodeBackward diodebackward_12 (.in(Deposit_WR_out), .out(diodebackward_11_out));
  not not_2 (nCE, _74540_1_pin15);
  PullUp pullup_5 (.out(diodebackward_11_out));
  PullUp pullup_6 (.out(pullup_6_out));
  DiodeBackward diodebackward_13 (.in(Deposit_WR_out), .out(pullup_6_out));
  not not_3 (nOE, _74540_1_pin17);
  not not_4 (nDE, _74540_1_pin16);
  nand nand_1 (UP, _74540_1_pin13, _74540_1_pin14);
  nand nand_2 (DN, _74540_1_pin12, _74540_1_pin14);
  PullUp pullup_7 (.out(pullup_7_out));
  DiodeBackward diodebackward_14 (.in(Clear_out), .out(diodebackward_14_out));
  DiodeBackward diodebackward_15 (.in(Examine_RD_out), .out(pullup_7_out));
  PullUp pullup_8 (.out(diodebackward_14_out));
  _74540 _74540_1 (
    .pin1(1'b0), .pin2(diodebackward_14_out), .pin3(pullup_7_out), .pin4(pullup_6_out),
    .pin5(diodebackward_11_out), .pin6(diodebackward_3_out), .pin7(pullup_3_out), .pin8(pullup_2_out),
    .pin9(diodebackward_1_out), .pin10(1'b0), .pin11(_74540_1_pin11), .pin12(_74540_1_pin12),
    .pin13(_74540_1_pin13), .pin14(_74540_1_pin14), .pin15(_74540_1_pin15), .pin16(_74540_1_pin16),
    .pin17(_74540_1_pin17), .pin18(RES), .pin19(1'b0), .pin20(1'b1));
  Seven_Seg_Hex seven_seg_hex_1 (.d({A15, A14, A13, A12}), .dp(1'b0));
  Button #(.activeLow("true")) Clear (.out(Clear_out));
  Button #(.activeLow("true")) Examine_RD (.out(Examine_RD_out));
  Button #(.activeLow("true")) Deposit_WR (.out(Deposit_WR_out));
  Button #(.activeLow("true")) Dec (.out(Dec_out));
  Button #(.activeLow("true")) Inc (.out(Inc_out));
  Button #(.activeLow("true")) Address (.out(Address_out));
  _74173 _74173_1 (
    .pin1(1'b0), .pin2(1'b0), .pin3(A12), .pin4(A13), .pin5(A14), .pin6(A15), .pin7(CLK), .pin8(1'b0),
    .pin9(1'b0), .pin10(1'b0), .pin11(A11), .pin12(A10), .pin13(A9), .pin14(A8), .pin15(1'b0), .pin16(1'b1));
  Seven_Seg_Hex seven_seg_hex_2 (.d({A11, A10, A9, A8}), .dp(1'b0));
  Seven_Seg_Hex seven_seg_hex_3 (.d({A7, A6, A5, A4}), .dp(1'b0));
  Seven_Seg_Hex seven_seg_hex_4 (.d({A3, A2, A1, A0}), .dp(1'b0));
  Button #(.activeLow("true")) C (.out(C_out));
  Button #(.activeLow("true")) _8 (.out(_8_out));
  Button #(.activeLow("true")) _4 (.out(_4_out));
  Button #(.activeLow("true")) _0 (.out(_0_out));
  _74173 _74173_2 (
    .pin1(1'b0), .pin2(1'b0), .pin3(A8), .pin4(A9), .pin5(A10), .pin6(A11), .pin7(CLK), .pin8(1'b0),
    .pin9(1'b0), .pin10(1'b0), .pin11(A7), .pin12(A6), .pin13(A5), .pin14(A4), .pin15(1'b0), .pin16(1'b1));
  Button #(.activeLow("true")) D (.out(D_out));
  Button #(.activeLow("true")) _9 (.out(_9_out));
  Button #(.activeLow("true")) _5 (.out(_5_out));
  Button #(.activeLow("true")) _1 (.out(_1_out));
  Seven_Seg_Hex seven_seg_hex_5 (.d({Q15, Q14, Q13, Q12}), .dp(1'b0));
  Seven_Seg_Hex seven_seg_hex_6 (.d({Q11, Q10, Q9, Q8}), .dp(1'b0));
  Button #(.activeLow("true")) E (.out(E_out));
  Button #(.activeLow("true")) A (.out(A_out));
  Button #(.activeLow("true")) _6 (.out(_6_out));
  Button #(.activeLow("true")) _2 (.out(_2_out));
  _74173 _74173_3 (
    .pin1(1'b0), .pin2(1'b0), .pin3(A4), .pin4(A5), .pin5(A6), .pin6(A7), .pin7(CLK), .pin8(1'b0),
    .pin9(1'b0), .pin10(1'b0), .pin11(A3), .pin12(A2), .pin13(A1), .pin14(A0), .pin15(1'b0), .pin16(1'b1));
  Seven_Seg_Hex seven_seg_hex_7 (.d({Q7, Q6, Q5, Q4}), .dp(1'b0));
  Seven_Seg_Hex seven_seg_hex_8 (.d({Q3, Q2, Q1, Q0}), .dp(1'b0));
  Button #(.activeLow("true")) F (.out(F_out));
  Button #(.activeLow("true")) B (.out(B_out));
  Button #(.activeLow("true")) _7 (.out(_7_out));
  Button #(.activeLow("true")) _3 (.out(_3_out));
  _74173 _74173_4 (
    .pin1(1'b0), .pin2(1'b0), .pin3(A0), .pin4(A1), .pin5(A2), .pin6(A3), .pin7(CLK), .pin8(1'b0),
    .pin9(1'b0), .pin10(1'b0), .pin11(_74173_4_pin11), .pin12(_74173_4_pin12), .pin13(_74173_4_pin13),
    .pin14(_74173_4_pin14), .pin15(1'b0), .pin16(1'b1));
  Seven_Seg_Hex seven_seg_hex_9 (.d({B15, B14, B13, B12}), .dp(1'b0));
  Seven_Seg_Hex seven_seg_hex_10 (.d({B11, B10, B9, B8}), .dp(1'b0));
  PullUp pullup_9 (.out(pullup_9_out));
  DiodeBackward diodebackward_16 (.in(F_out), .out(pullup_9_out));
  DiodeBackward diodebackward_17 (.in(E_out), .out(pullup_9_out));
  DiodeBackward diodebackward_18 (.in(D_out), .out(pullup_9_out));
  DiodeBackward diodebackward_19 (.in(C_out), .out(pullup_9_out));
  DiodeBackward diodebackward_20 (.in(B_out), .out(pullup_9_out));
  DiodeBackward diodebackward_21 (.in(A_out), .out(pullup_9_out));
  DiodeBackward diodebackward_22 (.in(_9_out), .out(pullup_9_out));
  DiodeBackward diodebackward_23 (.in(_8_out), .out(pullup_9_out));
  not not_5 (_74173_4_pin11, pullup_9_out);
  Seven_Seg_Hex seven_seg_hex_11 (.d({B7, B6, B5, B4}), .dp(1'b0));
  PullUp pullup_10 (.out(pullup_10_out));
  DiodeBackward diodebackward_24 (.in(F_out), .out(pullup_10_out));
  DiodeBackward diodebackward_25 (.in(F_out), .out(diodebackward_25_out));
  DiodeBackward diodebackward_26 (.in(E_out), .out(pullup_10_out));
  DiodeBackward diodebackward_27 (.in(E_out), .out(diodebackward_25_out));
  DiodeBackward diodebackward_28 (.in(D_out), .out(pullup_10_out));
  DiodeBackward diodebackward_29 (.in(C_out), .out(pullup_10_out));
  DiodeBackward diodebackward_30 (.in(B_out), .out(diodebackward_25_out));
  DiodeBackward diodebackward_31 (.in(A_out), .out(diodebackward_25_out));
  DiodeBackward diodebackward_32 (.in(_7_out), .out(pullup_10_out));
  DiodeBackward diodebackward_33 (.in(_7_out), .out(diodebackward_25_out));
  DiodeBackward diodebackward_34 (.in(_6_out), .out(pullup_10_out));
  DiodeBackward diodebackward_35 (.in(_6_out), .out(diodebackward_25_out));
  DiodeBackward diodebackward_36 (.in(_5_out), .out(pullup_10_out));
  DiodeBackward diodebackward_37 (.in(_4_out), .out(pullup_10_out));
  DiodeBackward diodebackward_38 (.in(_3_out), .out(diodebackward_25_out));
  DiodeBackward diodebackward_39 (.in(_2_out), .out(diodebackward_25_out));
  not not_6 (_74173_4_pin12, pullup_10_out);
  Seven_Seg_Hex seven_seg_hex_12 (.d({B3, B2, B1, B0}), .dp(1'b0));
  PullUp pullup_11 (.out(diodebackward_25_out));
  DiodeBackward diodebackward_40 (.in(F_out), .out(diodebackward_40_out));
  DiodeBackward diodebackward_41 (.in(D_out), .out(diodebackward_40_out));
  DiodeBackward diodebackward_42 (.in(B_out), .out(diodebackward_40_out));
  DiodeBackward diodebackward_43 (.in(_9_out), .out(diodebackward_40_out));
  DiodeBackward diodebackward_44 (.in(_7_out), .out(diodebackward_40_out));
  DiodeBackward diodebackward_45 (.in(_5_out), .out(diodebackward_40_out));
  DiodeBackward diodebackward_46 (.in(_3_out), .out(diodebackward_40_out));
  DiodeBackward diodebackward_47 (.in(_1_out), .out(diodebackward_40_out));
  not not_7 (_74173_4_pin13, diodebackward_25_out);
  PullUp pullup_12 (.out(diodebackward_40_out));
  PullUp pullup_13 (.out(pullup_13_out));
  DiodeBackward diodebackward_48 (.in(F_out), .out(pullup_13_out));
  DiodeBackward diodebackward_49 (.in(E_out), .out(pullup_13_out));
  DiodeBackward diodebackward_50 (.in(D_out), .out(pullup_13_out));
  DiodeBackward diodebackward_51 (.in(C_out), .out(pullup_13_out));
  DiodeBackward diodebackward_52 (.in(B_out), .out(pullup_13_out));
  DiodeBackward diodebackward_53 (.in(A_out), .out(pullup_13_out));
  DiodeBackward diodebackward_54 (.in(_9_out), .out(pullup_13_out));
  DiodeBackward diodebackward_55 (.in(_8_out), .out(pullup_13_out));
  DiodeBackward diodebackward_56 (.in(_7_out), .out(pullup_13_out));
  DiodeBackward diodebackward_57 (.in(_6_out), .out(pullup_13_out));
  DiodeBackward diodebackward_58 (.in(_5_out), .out(pullup_13_out));
  DiodeBackward diodebackward_59 (.in(_4_out), .out(pullup_13_out));
  DiodeBackward diodebackward_60 (.in(_3_out), .out(pullup_13_out));
  DiodeBackward diodebackward_61 (.in(_2_out), .out(pullup_13_out));
  DiodeBackward diodebackward_62 (.in(_1_out), .out(pullup_13_out));
  DiodeBackward diodebackward_63 (.in(_0_out), .out(pullup_13_out));
  not not_8 (_74173_4_pin14, diodebackward_40_out);
  not not_9 (not_9_out, pullup_13_out);
  not not_10 (CLK, not_9_out);
  _74193 _74193_1 (
    .pin1(A1), .pin2(Q1), .pin3(Q0), .pin4(DN), .pin5(UP), .pin6(Q2), .pin7(Q3), .pin8(1'b0), .pin9(A3),
    .pin10(A2), .pin11(nLD), .pin12(_74193_1_pin12), .pin13(_74193_1_pin13), .pin14(RES), .pin15(A0),
    .pin16(1'b1));
  _74193 _74193_2 (
    .pin1(A5), .pin2(Q5), .pin3(Q4), .pin4(_74193_1_pin13), .pin5(_74193_1_pin12), .pin6(Q6), .pin7(Q7),
    .pin8(1'b0), .pin9(A7), .pin10(A6), .pin11(nLD), .pin12(_74193_2_pin12), .pin13(_74193_2_pin13),
    .pin14(RES), .pin15(A4), .pin16(1'b1));
  _74193 _74193_3 (
    .pin1(A9), .pin2(Q9), .pin3(Q8), .pin4(_74193_2_pin13), .pin5(_74193_2_pin12), .pin6(Q10), .pin7(Q11),
    .pin8(1'b0), .pin9(A11), .pin10(A10), .pin11(nLD), .pin12(_74193_3_pin12), .pin13(_74193_3_pin13),
    .pin14(RES), .pin15(A8), .pin16(1'b1));
  _74193 _74193_4 (
    .pin1(A13), .pin2(Q13), .pin3(Q12), .pin4(_74193_3_pin13), .pin5(_74193_3_pin12), .pin6(Q14), .pin7(Q15),
    .pin8(1'b0), .pin9(A15), .pin10(A14), .pin11(nLD), .pin14(RES), .pin15(A12), .pin16(1'b1));  // open: pin12, pin13
  _62256 _62256_1 (
    .A0(Q0), .A1(Q1), .A2(Q2), .A3(Q3), .A4(Q4), .A5(Q5), .A6(Q6), .A7(Q7), .A8(Q8), .A9(Q9), .A10(Q10),
    .A11(Q11), .A12(Q12), .nCE(nCE), .nOE(nOE), .nWE(nDE), .D0(B8), .D1(B9), .D2(B10), .D3(B11), .D4(B12),
    .D5(B13), .D6(B14), .D7(B15), .VCC(1'b1), .GND(1'b0), .A13(Q13), .A14(Q14));
  _74541 _74541_1 (
    .pin1(nDE), .pin2(A15), .pin3(A14), .pin4(A13), .pin5(A12), .pin6(A11), .pin7(A10), .pin8(A9), .pin9(A8),
    .pin10(1'b0), .pin11(B8), .pin12(B9), .pin13(B10), .pin14(B11), .pin15(B12), .pin16(B13), .pin17(B14),
    .pin18(B15), .pin19(nDE), .pin20(1'b1));
  _62256 _62256_2 (
    .A0(Q0), .A1(Q1), .A2(Q2), .A3(Q3), .A4(Q4), .A5(Q5), .A6(Q6), .A7(Q7), .A8(Q8), .A9(Q9), .A10(Q10),
    .A11(Q11), .A12(Q12), .nCE(nCE), .nOE(nOE), .nWE(nDE), .D0(B0), .D1(B1), .D2(B2), .D3(B3), .D4(B4),
    .D5(B5), .D6(B6), .D7(B7), .VCC(1'b1), .GND(1'b0), .A13(Q13), .A14(Q14));
  _74541 _74541_2 (
    .pin1(nDE), .pin2(A7), .pin3(A6), .pin4(A5), .pin5(A4), .pin6(A3), .pin7(A2), .pin8(A1), .pin9(A0),
    .pin10(1'b0), .pin11(B0), .pin12(B1), .pin13(B2), .pin14(B3), .pin15(B4), .pin16(B5), .pin17(B6),
    .pin18(B7), .pin19(nDE), .pin20(1'b1));

  // Other names for the same wires on the sheet: nWE = nDE

  // Notes on the sheet:
  //   LOAD
  //   UP
  //   DOWN
  //   ~CE
  //   COUNT
  //   WRITE
  //   READ
  //   RESET
  //   KEY DATA
  //   KEYSWITCH REGISTER
  //   RAM ADDRESS
  //   RAM DATA
  //   PROGRAM COUNTER
  //   RAM HI
  //   DATA BUFFER HI
  //   DATA BUFFER LO
  //   RAM LO
endmodule
